// Logisim project final_redo.circ as structural Verilog: 8 circuits, main circuit DUT
module DUT (
  input  [7:0] X1,
  input  [7:0] Y1,
  input  [7:0] X2,
  input  [7:0] Y2,
  input  GO1,
  input  GO2,
  input  CLK,
  input  RST,
  output [11:0] DIST,
  output DONE
);

  wire [16:0] load_and_get_radicand_1_radicand;

  load_and_get_radicand load_and_get_radicand_1 (
    .CLK(CLK), .RST(RST), .X2(X2), .X1(X1), .Y2(Y2), .Y1(Y1), .GO1(GO1), .GO2(GO2),
    .radicand(load_and_get_radicand_1_radicand), .DONE(DONE));
  // Probe on load_and_get_radicand_1_radicand
  square_root_calculator square_root_calculator_1 (.in_1(load_and_get_radicand_1_radicand), .out_2(DIST));

  // Notes on the sheet:
  //   Please put your design below. You may also use subcircuits.
  //   However, do not move, rename, add, or delete any pins.
endmodule

module TB (
  input  [7:0] X1,
  input  [7:0] Y1,
  input  [7:0] X2,
  input  [7:0] Y2,
  input  GO1,
  input  GO2,
  input  RST,
  output [11:0] DIST,
  output DONE
);

  wire clk_out, or_1_out, RESET_out;

  Clock sysclk ();  // open: out
  Button RESET (.out(RESET_out));
  Clock #(.highDuration(2), .lowDuration(2)) clk (.out(clk_out));
  or or_1 (or_1_out, RESET_out, RST);
  DUT dut_1 (
    .X1(X1), .Y1(Y1), .X2(X2), .Y2(Y2), .GO1(GO1), .GO2(GO2), .CLK(clk_out), .RST(or_1_out), .DIST(DIST),
    .DONE(DONE));

  // Notes on the sheet:
  //   DO NOT MODIFY THIS
  //   YOU MAY TEST YOUR CIRCUITS USING THIS TO MAKE SURE YOU HAVE NOT ALTERED PIN OUT
endmodule

module load_and_get_radicand (
  input  CLK,
  input  RST,
  input  [7:0] X2,
  input  [7:0] X1,
  input  [7:0] Y2,
  input  [7:0] Y1,
  input  GO1,
  input  GO2,
  output [16:0] radicand,
  output DONE
);

  wire adder_5_cout, budgetand_1_out_3, budgetand_2_out_3, budgetand_4_out_3, budgetor_2_out_3,
       budgetor_3_out_3, not_1_out, not_4_out, rdy, register_5_q, register_6_q, rst_done;
  wire [7:0] register_1_q, register_2_q, register_3_q, register_4_q;
  wire [8:0] adder_1_out, adder_2_out, adder_3_out, adder_4_out, bit_extender_1_out, bit_extender_2_out,
       bit_extender_3_out, bit_extender_4_out, multiplier_1_cout, multiplier_1_out, multiplier_2_cout,
       multiplier_2_out, not_2_out, not_3_out;
  wire [15:0] adder_5_out, bit_normalization_1_out_3, bit_normalization_2_out_3;

  Register register_1 (.D(X2), .en(GO2), .clk(CLK), .Q(register_1_q));  // open: clr
  Register register_2 (.D(X1), .en(GO1), .clk(CLK), .Q(register_2_q));  // open: clr
  Register register_3 (.D(Y2), .en(GO2), .clk(CLK), .Q(register_3_q));  // open: clr
  Register register_4 (.D(Y1), .en(GO1), .clk(CLK), .Q(register_4_q));  // open: clr
  not not_1 (not_1_out, RST);
  budgetAND budgetand_1 (.in_1(GO1), .in_2(not_1_out), .out_3(budgetand_1_out_3));
  budgetAND budgetand_2 (.in_1(GO2), .in_2(not_1_out), .out_3(budgetand_2_out_3));
  budgetOR budgetor_1 (.in_1(RST), .in_2(DONE), .out_3(rst_done));
  budgetOR budgetor_2 (.in_1(rst_done), .in_2(GO1), .out_3(budgetor_2_out_3));
  budgetOR budgetor_3 (.in_1(rst_done), .in_2(GO2), .out_3(budgetor_3_out_3));
  assign bit_extender_1_out = {{1{register_1_q[7]}}, register_1_q};  // Bit_Extender bit_extender_1
  assign bit_extender_2_out = {{1{register_2_q[7]}}, register_2_q};  // Bit_Extender bit_extender_2
  assign bit_extender_3_out = {{1{register_3_q[7]}}, register_3_q};  // Bit_Extender bit_extender_3
  assign bit_extender_4_out = {{1{register_4_q[7]}}, register_4_q};  // Bit_Extender bit_extender_4
  assign not_2_out = ~bit_extender_2_out;  // NOT_Gate not_2, 9 bits wide
  Adder #(.width(9)) adder_1 (.a(not_2_out), .b(9'h1), .out(adder_1_out));  // open: cin, cout
  assign not_3_out = ~bit_extender_4_out;  // NOT_Gate not_3, 9 bits wide
  Adder #(.width(9)) adder_2 (.a(not_3_out), .b(9'h1), .out(adder_2_out));  // open: cin, cout
  Register #(.width(1)) register_5 (
    .D(budgetand_1_out_3), .en(budgetor_2_out_3), .clk(CLK), .Q(register_5_q));  // open: clr
  Register #(.width(1)) register_6 (
    .D(budgetand_2_out_3), .en(budgetor_3_out_3), .clk(CLK), .Q(register_6_q));  // open: clr
  budgetAND budgetand_3 (.in_1(register_5_q), .in_2(register_6_q), .out_3(rdy));
  Adder #(.width(9)) adder_3 (.a(bit_extender_1_out), .b(adder_1_out), .out(adder_3_out));  // open: cin, cout
  Adder #(.width(9)) adder_4 (.a(bit_extender_3_out), .b(adder_2_out), .out(adder_4_out));  // open: cin, cout
  Multiplier #(.mode("twosComplement"), .width(9)) multiplier_1 (
    .a(adder_3_out), .b(adder_3_out), .out(multiplier_1_out), .cout(multiplier_1_cout));  // open: cin
  Multiplier #(.mode("twosComplement"), .width(9)) multiplier_2 (
    .a(adder_4_out), .b(adder_4_out), .out(multiplier_2_out), .cout(multiplier_2_cout));  // open: cin
  not not_4 (not_4_out, rst_done);
  budgetAND budgetand_4 (.in_1(not_4_out), .in_2(rdy), .out_3(budgetand_4_out_3));
  bit_normalization bit_normalization_1 (
    .in_1(multiplier_1_out), .c_over(multiplier_1_cout), .out_3(bit_normalization_1_out_3));
  bit_normalization bit_normalization_2 (
    .in_1(multiplier_2_out), .c_over(multiplier_2_cout), .out_3(bit_normalization_2_out_3));
  D_Flip_Flop d_ff_1 (.D(budgetand_4_out_3), .clk(CLK), .Q(DONE));  // open: Qn, preset, reset
  Adder #(.width(16)) adder_5 (
    .a(bit_normalization_1_out_3), .b(bit_normalization_2_out_3), .out(adder_5_out), .cout(adder_5_cout));  // open: cin
  sixteen_to_17 sixteen_to_17_1 (.in_1(adder_5_out), .in_2(adder_5_cout), .out_3(radicand));

  // Notes on the sheet:
  //   load in values
  //   can I start calculating distance?
  //   the number that should be square rooted
endmodule

module budgetAND (
  input  in_1,
  input  in_2,
  output out_3
);

  wire nand_1_out;

  nand nand_1 (nand_1_out, in_1, in_2);
  not not_1 (out_3, nand_1_out);
endmodule

module budgetOR (
  input  in_1,
  input  in_2,
  output out_3
);

  wire not_1_out, not_2_out;

  not not_1 (not_1_out, in_1);
  not not_2 (not_2_out, in_2);
  nand nand_1 (out_3, not_1_out, not_2_out);
endmodule

module bit_normalization (
  input  [8:0] in_1,
  input  [8:0] c_over,
  output [15:0] out_3
);


  assign out_3 = {c_over[6:0], in_1};
endmodule

module sixteen_to_17 (
  input  [15:0] in_1,
  input  in_2,
  output [16:0] out_3
);


  assign out_3 = {in_2, in_1};
endmodule

module square_root_calculator (
  input  [16:0] in_1,
  output [11:0] out_2
);

  wire subtractor_1_bout, subtractor_2_bout, subtractor_3_bout, subtractor_4_bout, subtractor_5_bout,
       subtractor_6_bout, subtractor_7_bout, subtractor_8_bout, subtractor_9_bout, subtractor_10_bout,
       subtractor_11_bout;
  wire [1:0] bit_extender_1_out, multiplexer_1_out;
  wire [2:0] bit_extender_2_out, bit_extender_3_out, multiplexer_2_out, subtractor_1_out;
  wire [3:0] bit_extender_4_out, bit_extender_5_out, multiplexer_3_out, subtractor_2_out;
  wire [4:0] bit_extender_6_out, bit_extender_7_out, multiplexer_4_out, subtractor_3_out;
  wire [5:0] bit_extender_8_out, bit_extender_9_out, subtractor_4_out;
  wire [6:0] bit_extender_10_out, bit_extender_11_out, multiplexer_6_out, subtractor_5_out;
  wire [7:0] bit_extender_12_out, bit_extender_13_out, multiplexer_7_out, subtractor_6_out;
  wire [7:2] multiplexer_5_out;
  wire [8:0] bit_extender_14_out, bit_extender_15_out, multiplexer_8_out, subtractor_7_out;
  wire [9:0] bit_extender_16_out, bit_extender_17_out, multiplexer_9_out, subtractor_8_out;
  wire [10:0] bit_extender_18_out, bit_extender_19_out, multiplexer_10_out, subtractor_9_out;
  wire [11:0] subtractor_10_out;
  wire [12:0] subtractor_11_out;

  not not_1 (out_2[10], subtractor_1_bout);
  not not_2 (out_2[9], subtractor_2_bout);
  Bit_Extender #(.in_width(3), .out_width(2), .\type ("zero")) bit_extender_1 (
    .in(subtractor_1_out), .out(bit_extender_1_out));
  Subtractor #(.width(3)) subtractor_1 (
    .a({1'b0, in_1[15:14]}), .b({in_1[16], 2'b01}), .out(subtractor_1_out), .bout(subtractor_1_bout));  // open: bin
  Multiplexer #(.width(2)) multiplexer_1 (
    .in0(in_1[15:14]), .in1(bit_extender_1_out), .out(multiplexer_1_out), .sel(out_2[10]));
  not not_3 (out_2[8], subtractor_3_bout);
  not not_4 (out_2[7], subtractor_4_bout);
  not not_5 (out_2[6], subtractor_5_bout);
  not not_6 (out_2[5], subtractor_6_bout);
  not not_7 (out_2[4], subtractor_7_bout);
  not not_8 (out_2[3], subtractor_8_bout);
  not not_9 (out_2[2], subtractor_9_bout);
  not not_10 (out_2[1], subtractor_10_bout);
  not not_11 (out_2[0], subtractor_11_bout);
  Subtractor #(.width(4)) subtractor_2 (
    .a({multiplexer_1_out, in_1[13:12]}), .b({in_1[16], out_2[10], 2'b01}), .out(subtractor_2_out),
    .bout(subtractor_2_bout));  // open: bin
  Bit_Extender #(.in_width(4), .out_width(3), .\type ("zero")) bit_extender_2 (
    .in({multiplexer_1_out, in_1[13:12]}), .out(bit_extender_2_out));
  Bit_Extender #(.in_width(4), .out_width(3), .\type ("zero")) bit_extender_3 (
    .in(subtractor_2_out), .out(bit_extender_3_out));
  Multiplexer #(.width(3)) multiplexer_2 (
    .in0(bit_extender_2_out), .in1(bit_extender_3_out), .out(multiplexer_2_out), .sel(out_2[9]));
  Subtractor #(.width(5)) subtractor_3 (
    .a({multiplexer_2_out, in_1[11:10]}), .b({in_1[16], out_2[10:9], 2'b01}), .out(subtractor_3_out),
    .bout(subtractor_3_bout));  // open: bin
  Bit_Extender #(.in_width(5), .out_width(4)) bit_extender_4 (
    .in({multiplexer_2_out, in_1[11:10]}), .out(bit_extender_4_out));
  Multiplexer #(.width(4)) multiplexer_3 (
    .in0(bit_extender_4_out), .in1(bit_extender_5_out), .out(multiplexer_3_out), .sel(out_2[8]));
  Bit_Extender #(.in_width(5), .out_width(4), .\type ("zero")) bit_extender_5 (
    .in(subtractor_3_out), .out(bit_extender_5_out));
  Bit_Extender #(.in_width(6), .out_width(5), .\type ("zero")) bit_extender_6 (
    .in(subtractor_4_out), .out(bit_extender_6_out));
  Subtractor #(.width(6)) subtractor_4 (
    .a({multiplexer_3_out, in_1[9:8]}), .b({in_1[16], out_2[10:8], 2'b01}), .out(subtractor_4_out),
    .bout(subtractor_4_bout));  // open: bin
  Bit_Extender #(.in_width(6), .out_width(5), .\type ("zero")) bit_extender_7 (
    .in({multiplexer_3_out, in_1[9:8]}), .out(bit_extender_7_out));
  Multiplexer #(.width(5)) multiplexer_4 (
    .in0(bit_extender_7_out), .in1(bit_extender_6_out), .out(multiplexer_4_out), .sel(out_2[7]));
  Subtractor #(.width(7)) subtractor_5 (
    .a({multiplexer_4_out, in_1[7:6]}), .b({in_1[16], out_2[10:7], 2'b01}), .out(subtractor_5_out),
    .bout(subtractor_5_bout));  // open: bin
  Bit_Extender #(.in_width(7), .out_width(6), .\type ("zero")) bit_extender_8 (
    .in({multiplexer_4_out, in_1[7:6]}), .out(bit_extender_8_out));
  Multiplexer #(.width(6)) multiplexer_5 (
    .in0(bit_extender_8_out), .in1(bit_extender_9_out), .out(multiplexer_5_out), .sel(out_2[6]));
  Bit_Extender #(.in_width(7), .out_width(6), .\type ("zero")) bit_extender_9 (
    .in(subtractor_5_out), .out(bit_extender_9_out));
  Bit_Extender #(.out_width(7), .\type ("zero")) bit_extender_10 (.in(subtractor_6_out), .out(bit_extender_10_out));
  Subtractor subtractor_6 (
    .a({multiplexer_5_out, in_1[5:4]}), .b({in_1[16], out_2[10:6], 2'b01}), .out(subtractor_6_out),
    .bout(subtractor_6_bout));  // open: bin
  Bit_Extender #(.out_width(7), .\type ("zero")) bit_extender_11 (
    .in({multiplexer_5_out, in_1[5:4]}), .out(bit_extender_11_out));
  Multiplexer #(.width(7)) multiplexer_6 (
    .in0(bit_extender_11_out), .in1(bit_extender_10_out), .out(multiplexer_6_out), .sel(out_2[5]));
  Bit_Extender #(.in_width(9), .out_width(8), .\type ("zero")) bit_extender_12 (
    .in(subtractor_7_out), .out(bit_extender_12_out));
  Subtractor #(.width(9)) subtractor_7 (
    .a({multiplexer_6_out, in_1[3:2]}), .b({in_1[16], out_2[10:5], 2'b01}), .out(subtractor_7_out),
    .bout(subtractor_7_bout));  // open: bin
  Bit_Extender #(.in_width(9), .out_width(8), .\type ("zero")) bit_extender_13 (
    .in({multiplexer_6_out, in_1[3:2]}), .out(bit_extender_13_out));
  Multiplexer #(.width(8)) multiplexer_7 (
    .in0(bit_extender_13_out), .in1(bit_extender_12_out), .out(multiplexer_7_out), .sel(out_2[4]));
  Subtractor #(.width(10)) subtractor_8 (
    .a({multiplexer_7_out, in_1[1:0]}), .b({in_1[16], out_2[10:4], 2'b01}), .out(subtractor_8_out),
    .bout(subtractor_8_bout));  // open: bin
  Bit_Extender #(.in_width(10), .out_width(9), .\type ("zero")) bit_extender_14 (
    .in({multiplexer_7_out, in_1[1:0]}), .out(bit_extender_14_out));
  Multiplexer #(.width(9)) multiplexer_8 (
    .in0(bit_extender_14_out), .in1(bit_extender_15_out), .out(multiplexer_8_out), .sel(out_2[3]));
  Bit_Extender #(.in_width(10), .out_width(9), .\type ("zero")) bit_extender_15 (
    .in(subtractor_8_out), .out(bit_extender_15_out));
  Bit_Extender #(.in_width(11), .out_width(10), .\type ("zero")) bit_extender_16 (
    .in(subtractor_9_out), .out(bit_extender_16_out));
  Subtractor #(.width(11)) subtractor_9 (
    .a({multiplexer_8_out, 2'b00}), .b({in_1[16], out_2[10:3], 2'b01}), .out(subtractor_9_out),
    .bout(subtractor_9_bout));  // open: bin
  Bit_Extender #(.in_width(11), .out_width(10), .\type ("zero")) bit_extender_17 (
    .in({multiplexer_8_out, 2'b00}), .out(bit_extender_17_out));
  Multiplexer #(.width(10)) multiplexer_9 (
    .in0(bit_extender_17_out), .in1(bit_extender_16_out), .out(multiplexer_9_out), .sel(out_2[2]));
  Bit_Extender #(.in_width(12), .out_width(11), .\type ("zero")) bit_extender_18 (
    .in(subtractor_10_out), .out(bit_extender_18_out));
  Subtractor #(.width(12)) subtractor_10 (
    .a({multiplexer_9_out, 2'b00}), .b({in_1[16], out_2[10:2], 2'b01}), .out(subtractor_10_out),
    .bout(subtractor_10_bout));  // open: bin
  Bit_Extender #(.in_width(12), .out_width(11), .\type ("zero")) bit_extender_19 (
    .in({multiplexer_9_out, 2'b00}), .out(bit_extender_19_out));
  Multiplexer #(.width(11)) multiplexer_10 (
    .in0(bit_extender_19_out), .in1(bit_extender_18_out), .out(multiplexer_10_out), .sel(out_2[1]));
  Subtractor #(.width(13)) subtractor_11 (
    .a({multiplexer_10_out, 2'b00}), .b({in_1[16], out_2[10:1], 2'b01}), .out(subtractor_11_out),
    .bout(subtractor_11_bout));  // open: bin
  Bit_Extender #(.in_width(13), .out_width(12), .\type ("zero")) bit_extender_20 (.in(subtractor_11_out));  // open: out

  assign out_2[11] = in_1[16];

  // Other names for the same wires on the sheet: BG2[1:0] = in_1[13:12]; BG3[1:0] = in_1[11:10]; BG4[1:0] = in_1[9:8];
  //   BG5[1:0] = in_1[7:6]; BG6[1:0] = in_1[5:4]; BG7[1:0] = in_1[3:2]; BG8[1:0] = in_1[1:0]; D0 = out_2[0];
  //   D1 = out_2[1]; D2 = out_2[2]; Q0 = out_2[3]; Q1 = out_2[4]; Q2 = out_2[5]; Q3 = out_2[6]; Q4 = out_2[7];
  //   Q5 = out_2[8]; Q6 = out_2[9]; Q7 = out_2[10]; Q8 = in_1[16]

  // Notes on the sheet:
  //   BG - bit group, grouping the bits into pairs to use non-restoring square root algorithm
  //   non-restoring square root algo: use subtraction and shifts to find each bit of the root of input
  //   actual number
  //   three decimal points of accuracy
  //   output:
endmodule
