// Logisim project final_task1.circ as structural Verilog: 23 circuits, main circuit DUT
module DUT (
  input  [7:0] X1,
  input  [7:0] Y1,
  input  [7:0] X2,
  input  [7:0] Y2,
  input  GO1,
  input  GO2,
  input  CLK,
  input  RST,
  output [11:0] DIST,
  output DONE
);

  wire DONE_t, eq, found, gt, lt, nand_1_out, Q0, Q0a, Q0an, Q0n, Q1, Q1a, Q1an, Q1n, rdy;
  wire [3:0] af, aff;
  wire [8:0] awh, awhf;
  wire [16:0] num;

  D_Flip_Flop d_ff_1 (.D(Q1n), .clk(CLK), .Q(Q1));  // open: Qn, preset, reset
  D_Flip_Flop d_ff_2 (.D(Q0n), .clk(CLK), .Q(Q0));  // open: Qn, preset, reset
  D_Flip_Flop d_ff_3 (.D(Q1an), .clk(CLK), .Q(Q1a));  // open: Qn, preset, reset
  D_Flip_Flop d_ff_4 (.D(Q0an), .clk(CLK), .Q(Q0a));  // open: Qn, preset, reset
  nand nand_1 (nand_1_out, eq, lt, rdy);
  unifier unifier_1 (.in_1(aff), .in_2(awhf), .out_3(DIST));
  not not_1 (DONE, nand_1_out);
  // Probe on awh
  sq_controller sq_controller_1 (
    .Q1(Q1), .Q0(Q0), .RST(RST), .eq(eq), .rdy(rdy), .gt(gt), .Q1n(Q1n), .Q0n(Q0n), .found(found));
  datapath datapath_1 (
    .CLK(CLK), .RST(RST), .X2(X2), .X1(X1), .Y2(Y2), .Y1(Y1), .GO1(GO1), .GO2(GO2), .eq(eq), .awh(awh),
    .rdy(rdy), .af(af), .gt(gt), .num(num));
  accuracy_controller accuracy_controller_1 (
    .Q1(Q1a), .Q0(Q0a), .RST(RST), .lt(lt), .rdy(found), .Q1n(Q1an), .Q0n(Q0an), .done(DONE_t));
  the_precisioner the_precisioner_1 (
    .DONE(DONE_t), .RST(eq), .eq(RST), .awh(awh), .af(af), .num(num), .CLK(CLK), .awhn(awhf), .afn(aff),
    .lt(lt));
  // Probe on af

  // Notes on the sheet:
  //   Please put your design below. You may also use subcircuits.
  //   However, do not move, rename, add, or delete any pins.
endmodule

module TB (
  input  [7:0] X1,
  input  [7:0] Y1,
  input  [7:0] X2,
  input  [7:0] Y2,
  input  GO1,
  input  GO2,
  input  RST,
  output [11:0] DIST,
  output DONE
);

  wire clk_out, or_1_out, RESET_out;

  Clock sysclk ();  // open: out
  Button RESET (.out(RESET_out));
  Clock #(.highDuration(2), .lowDuration(2)) clk (.out(clk_out));
  or or_1 (or_1_out, RESET_out, RST);
  DUT dut_1 (
    .X1(X1), .Y1(Y1), .X2(X2), .Y2(Y2), .GO1(GO1), .GO2(GO2), .CLK(clk_out), .RST(or_1_out), .DIST(DIST),
    .DONE(DONE));

  // Notes on the sheet:
  //   DO NOT MODIFY THIS
  //   YOU MAY TEST YOUR CIRCUITS USING THIS TO MAKE SURE YOU HAVE NOT ALTERED PIN OUT
endmodule

module testing (
  input  [2:0] in_1,
  input  [2:0] in_2,
  input  [2:0] in_3,
  input  [2:0] in_4,
  input  [2:0] in_5,
  input  [5:0] in_6,
  input  [5:0] in_7,
  input  [5:0] in_8,
  input  [5:0] in_9,
  input  [5:0] in_10,
  input  [7:0] in_11,
  input  [3:0] in_12,
  input  [3:0] in_13,
  input  [3:0] in_14,
  input  [3:0] in_15,
  input  [3:0] whole1,
  input  [3:0] whole2,
  input  [2:0] frac1,
  input  [2:0] frac2
);

  wire adder_1_cout, adder_2_cout, adder_3_cout, adder_4_cout, comparator_1_lt;
  wire [2:0] adder_3_out, adder_4_out, multiplier_3_cout, multiplier_3_out, multiplier_4_cout,
       multiplier_4_out;
  wire [3:0] adder_1_out, adder_2_out, bit_extender_1_out, bit_extender_2_out, bit_extender_3_out,
       multiplier_5_out, multiplier_6_out, multiplier_7_out;
  wire [5:0] multiplier_1_cout, multiplier_1_out;
  wire [5:3] undriven;
  wire [7:0] multiplier_2_cout, multiplier_2_out;

  Multiplier #(.width(6)) multiplier_1 (
    .a(in_7), .b(in_7), .out(multiplier_1_out), .cout(multiplier_1_cout));  // open: cin
  Multiplier multiplier_2 (.a(in_11), .b(in_11), .out(multiplier_2_out), .cout(multiplier_2_cout));  // open: cin
  Adder #(.width(4)) adder_1 (.a(in_13), .b(in_15), .out(adder_1_out), .cout(adder_1_cout));  // open: cin
  Adder #(.width(4)) adder_2 (.a(in_12), .b(in_14), .out(adder_2_out), .cin(adder_1_cout), .cout(adder_2_cout));
  Multiplier #(.width(3)) multiplier_3 (
    .a(frac1), .b(frac2), .out(multiplier_3_out), .cout(multiplier_3_cout));  // open: cin
  Multiplier #(.width(3)) multiplier_4 (
    .a(in_1), .b(in_1), .out(multiplier_4_out), .cout(multiplier_4_cout));  // open: cin
  Adder #(.width(3)) adder_3 (.a(in_3), .b(in_5), .out(adder_3_out), .cout(adder_3_cout));  // open: cin
  // Probe on adder_4_cout
  Adder #(.width(3)) adder_4 (.a(in_2), .b(in_4), .out(adder_4_out), .cin(adder_3_cout), .cout(adder_4_cout));
  // Probe on multiplier_1_cout
  Comparator #(.mode("unsigned"), .width(6)) comparator_1 (.a(in_9), .b(in_10), .lt(comparator_1_lt));  // open: gt, eq
  // Probe on multiplier_2_cout
  // Probe on adder_2_cout
  assign bit_extender_1_out = {{1{1'b0}}, frac2};  // Bit_Extender bit_extender_1
  assign bit_extender_2_out = {{1{1'b0}}, frac1};  // Bit_Extender bit_extender_2
  // Probe on multiplier_3_cout
  // Probe on multiplier_4_out
  // Probe on multiplier_4_cout
  // Probe on adder_4_out
  // Probe on multiplier_1_out[5:3]
  // Probe on {1'b0, in_8[5:1]}
  // Probe on multiplier_2_out[7:4]
  // Probe on adder_2_out
  // Probe on adder_3_out
  // Probe on adder_1_out
  Multiplier #(.width(4)) multiplier_5 (.a(whole1), .b(whole2), .out(multiplier_5_out));  // open: cin, cout
  Multiplier #(.width(4)) multiplier_6 (.a(bit_extender_1_out), .b(whole1), .out(multiplier_6_out));  // open: cin, cout
  Multiplier #(.width(4)) multiplier_7 (.a(bit_extender_2_out), .b(whole2), .out(multiplier_7_out));  // open: cin, cout
  assign bit_extender_3_out = {{1{1'b0}}, multiplier_3_out};  // Bit_Extender bit_extender_3
  // Probe on {3'b000, undriven}
  Adder #(.width(4)) adder_5 (.a(multiplier_6_out), .b(multiplier_5_out));  // open: out, cin, cout
  Comparator #(.mode("unsigned"), .width(6)) comparator_2 (.a(in_6), .b({3'b000, undriven}));  // open: gt, eq, lt
  Adder #(.width(4)) adder_6 ();  // open: a, b, out, cin, cout
endmodule

module datapath (
  input  CLK,
  input  RST,
  input  [7:0] X2,
  input  [7:0] X1,
  input  [7:0] Y2,
  input  [7:0] Y1,
  input  GO1,
  input  GO2,
  output eq,
  output [8:0] awh,
  output rdy,
  output [3:0] af,
  output gt,
  output [16:0] num
);

  wire adder_5_cout, adder_7_cout, budgetand_1_out_3, budgetand_2_out_3, budgetand_3_out_3,
       budgetand_4_out_3, budgetand_5_out_3, budgetand_6_out_3, budgetand_8_out_3, budgetand_9_out_3,
       budgetand_10_out_3, budgetor_2_out_3, budgetor_3_out_3, budgetor_4_out_3, budgetor_5_out_3,
       budgetor_7_out_3, budgetor_8_out_3, budgetor_9_out_3, budgetor_10_out_3, budgetor_11_out_3,
       budgetor_12_out_3, budgetor_13_out_3, comparator_1_gt, comparator_2_eq, comparator_2_gt,
       comparator_3_eq, d_ff_1_q, d_ff_2_q, d_ff_3_q, g, lt, nand_1_out, nand_4_out, not_1_out, not_5_out,
       not_8_out, not_9_out, not_10_out, not_11_out, not_12_out, not_13_out, not_14_out, not_15_out,
       not_16_out, not_17_out, not_18_out, register_1_q, register_2_q, register_7_q, rst_done, sel_lock;
  wire [3:0] adder_7_out, bit_extender_6_out, bit_extender_12_out, end_frac, m_frac, nand_3_out, nand_6_out,
       not_7_out, not_20_out, start_frac;
  wire [8:0] adder_1_out, adder_2_out, adder_3_out, adder_4_out, bit_extender_1_out, bit_extender_2_out,
       bit_extender_3_out, bit_extender_4_out, bit_extender_11_out, multiplier_1_cout, multiplier_1_out,
       multiplier_2_cout, multiplier_2_out, nand_5_out, not_2_out, not_3_out, not_19_out, register_3_q,
       register_4_q, sixteen_to_9_1_out_2;
  wire [15:0] add_1_1_out_2, adder_5_out, adder_6_out, bit_extender_5_out, bit_normalization_1_out_3,
       bit_normalization_2_out_3, m_square_1_whole, m_whole, nand_2_out, not_6_out, register_5_q, start_whole;
  wire [16:0] adder_8_out, bit_extender_7_out, bit_extender_8_out, bit_extender_9_out, bit_extender_10_out,
       end_whole;

  assign bit_extender_1_out = {{1{X2[7]}}, X2};  // Bit_Extender bit_extender_1
  assign bit_extender_2_out = {{1{X1[7]}}, X1};  // Bit_Extender bit_extender_2
  assign bit_extender_3_out = {{1{Y2[7]}}, Y2};  // Bit_Extender bit_extender_3
  assign bit_extender_4_out = {{1{Y1[7]}}, Y1};  // Bit_Extender bit_extender_4
  not not_1 (not_1_out, RST);
  budgetAND budgetand_1 (.in_1(GO1), .in_2(not_1_out), .out_3(budgetand_1_out_3));
  budgetAND budgetand_2 (.in_1(GO2), .in_2(not_1_out), .out_3(budgetand_2_out_3));
  assign not_2_out = ~bit_extender_2_out;  // NOT_Gate not_2, 9 bits wide
  assign not_3_out = ~bit_extender_4_out;  // NOT_Gate not_3, 9 bits wide
  budgetOR budgetor_1 (.in_1(RST), .in_2(eq), .out_3(rst_done));
  Adder #(.width(9)) adder_1 (.a(not_2_out), .b(9'h1), .out(adder_1_out));  // open: cin, cout
  Adder #(.width(9)) adder_2 (.a(not_3_out), .b(9'h1), .out(adder_2_out));  // open: cin, cout
  budgetOR budgetor_2 (.in_1(rst_done), .in_2(GO1), .out_3(budgetor_2_out_3));
  budgetOR budgetor_3 (.in_1(rst_done), .in_2(GO2), .out_3(budgetor_3_out_3));
  Adder #(.width(9)) adder_3 (.a(bit_extender_1_out), .b(adder_1_out), .out(adder_3_out));  // open: cin, cout
  Adder #(.width(9)) adder_4 (.a(bit_extender_3_out), .b(adder_2_out), .out(adder_4_out));  // open: cin, cout
  Register #(.width(1)) register_1 (
    .D(budgetand_1_out_3), .en(budgetor_2_out_3), .clk(CLK), .Q(register_1_q));  // open: clr
  Register #(.width(1)) register_2 (
    .D(budgetand_2_out_3), .en(budgetor_3_out_3), .clk(CLK), .Q(register_2_q));  // open: clr
  Register #(.width(9)) register_3 (.D(adder_3_out), .en(rdy), .clk(CLK), .Q(register_3_q));  // open: clr
  Register #(.width(9)) register_4 (.D(adder_4_out), .en(rdy), .clk(CLK), .Q(register_4_q));  // open: clr
  not not_4 (rdy, nand_1_out);
  nand nand_1 (nand_1_out, register_1_q, register_2_q);
  Multiplier #(.mode("twosComplement"), .width(9)) multiplier_1 (
    .a(register_3_q), .b(register_3_q), .out(multiplier_1_out), .cout(multiplier_1_cout));  // open: cin
  Multiplier #(.mode("twosComplement"), .width(9)) multiplier_2 (
    .a(register_4_q), .b(register_4_q), .out(multiplier_2_out), .cout(multiplier_2_cout));  // open: cin
  not not_5 (not_5_out, rst_done);
  bit_normalization bit_normalization_1 (
    .in_1(multiplier_1_out), .c_over(multiplier_1_cout), .out_3(bit_normalization_1_out_3));
  bit_normalization bit_normalization_2 (
    .in_1(multiplier_2_out), .c_over(multiplier_2_cout), .out_3(bit_normalization_2_out_3));
  assign bit_extender_5_out = {{15{not_5_out}}, not_5_out};  // Bit_Extender bit_extender_5
  assign bit_extender_6_out = {{3{not_5_out}}, not_5_out};  // Bit_Extender bit_extender_6
  Adder #(.width(16)) adder_5 (
    .a(bit_normalization_1_out_3), .b(bit_normalization_2_out_3), .out(adder_5_out), .cout(adder_5_cout));  // open: cin
  Adder #(.width(16)) adder_6 (.a(m_whole), .b({16{1'b1}}), .out(adder_6_out));  // open: cin, cout
  add_1 add_1_1 (.in_1(m_whole), .out_2(add_1_1_out_2));
  Register #(.width(16)) register_5 (.D(adder_6_out), .en(g), .clk(CLK), .Q(register_5_q));  // open: clr
  sixteen_to_17 sixteen_to_17_1 (.in_1(adder_5_out), .in_2(adder_5_cout), .out_3(num));
  assign nand_2_out = ~(bit_extender_5_out & add_1_1_out_2);  // NAND_Gate nand_2, 16 bits wide
  assign not_6_out = ~nand_2_out;  // NOT_Gate not_6, 16 bits wide
  budgetOR budgetor_4 (.in_1(lt), .in_2(rst_done), .out_3(budgetor_4_out_3));
  assign nand_3_out = ~(bit_extender_6_out & m_frac);  // NAND_Gate nand_3, 4 bits wide
  assign not_7_out = ~nand_3_out;  // NOT_Gate not_7, 4 bits wide
  budgetOR budgetor_5 (.in_1(lt), .in_2(rst_done), .out_3(budgetor_5_out_3));
  // Probe on num
  Register #(.width(4)) u_end_frac (.D(m_frac), .en(g), .clk(CLK), .Q(end_frac));  // open: clr
  Register #(.width(16)) register_6 (.D(not_6_out), .en(budgetor_4_out_3), .clk(CLK), .Q(start_whole));  // open: clr
  Register #(.width(4)) u_start_frac (.D(not_7_out), .en(budgetor_5_out_3), .clk(CLK), .Q(start_frac));  // open: clr
  assign bit_extender_7_out = {{1{1'b0}}, register_5_q};  // Bit_Extender bit_extender_7
  // Probe on bit_extender_7_out
  Multiplexer #(.width(17)) multiplexer_1 (.in0(num), .in1(bit_extender_7_out), .out(end_whole), .sel(sel_lock));
  Adder #(.width(4)) adder_7 (.a(end_frac), .b(start_frac), .out(adder_7_out), .cout(adder_7_cout));  // open: cin
  assign bit_extender_8_out = {{1{1'b0}}, start_whole};  // Bit_Extender bit_extender_8
  Adder #(.width(17)) adder_8 (
    .a(end_whole), .b(bit_extender_8_out), .out(adder_8_out), .cin(adder_7_cout));  // open: cout
  div_by_2 div_by_2_1 (.in_1(adder_8_out), .f(adder_7_out), .fout(m_frac), .out_4(m_whole));
  // Probe on m_whole
  not not_8 (not_8_out, rst_done);
  // Probe on m_frac
  not not_9 (not_9_out, lt);
  budgetAND budgetand_3 (.in_1(not_8_out), .in_2(rdy), .out_3(budgetand_3_out_3));
  budgetAND budgetand_4 (.in_1(not_9_out), .in_2(budgetand_3_out_3), .out_3(budgetand_4_out_3));
  assign bit_extender_9_out = {{1{1'b0}}, start_whole};  // Bit_Extender bit_extender_9
  Comparator #(.mode("unsigned"), .width(4)) comparator_1 (
    .a(start_frac), .b(end_frac), .gt(comparator_1_gt));  // open: eq, lt
  budgetAND budgetand_5 (.in_1(not_8_out), .in_2(budgetand_4_out_3), .out_3(budgetand_5_out_3));
  // Probe on m_square_1_whole
  m_square m_square_1 (.in_1(m_whole), .f(m_frac), .whole(m_square_1_whole));  // open: frac
  Comparator #(.mode("unsigned"), .width(17)) comparator_2 (
    .a(bit_extender_9_out), .b(end_whole), .gt(comparator_2_gt), .eq(comparator_2_eq));  // open: lt
  D_Flip_Flop d_ff_1 (.D(budgetand_5_out_3), .clk(CLK), .Q(d_ff_1_q));  // open: Qn, preset, reset
  assign bit_extender_10_out = {{1{1'b0}}, m_square_1_whole};  // Bit_Extender bit_extender_10
  budgetAND budgetand_6 (.in_1(comparator_2_eq), .in_2(comparator_1_gt), .out_3(budgetand_6_out_3));
  Comparator #(.mode("unsigned"), .width(17)) comparator_3 (
    .a(bit_extender_10_out), .b(num), .gt(g), .eq(comparator_3_eq), .lt(lt));
  budgetOR budgetor_6 (.in_1(comparator_2_gt), .in_2(budgetand_6_out_3), .out_3(gt));
  budgetAND budgetand_7 (.in_1(d_ff_1_q), .in_2(comparator_3_eq), .out_3(eq));
  D_Flip_Flop d_ff_2 (.D(comparator_3_eq), .clk(CLK), .Q(d_ff_2_q));  // open: Qn, preset, reset
  D_Flip_Flop d_ff_3 (.D(gt), .clk(CLK), .Q(d_ff_3_q));  // open: Qn, preset, reset
  budgetOR budgetor_7 (.in_1(lt), .in_2(comparator_3_eq), .out_3(budgetor_7_out_3));
  budgetOR budgetor_8 (.in_1(comparator_3_eq), .in_2(lt), .out_3(budgetor_8_out_3));
  not not_10 (not_10_out, eq);
  not not_11 (not_11_out, budgetor_7_out_3);
  not not_12 (not_12_out, RST);
  not not_13 (not_13_out, RST);
  budgetOR budgetor_9 (.in_1(eq), .in_2(RST), .out_3(budgetor_9_out_3));
  budgetOR budgetor_10 (.in_1(RST), .in_2(budgetor_8_out_3), .out_3(budgetor_10_out_3));
  budgetOR budgetor_11 (.in_1(RST), .in_2(budgetor_8_out_3), .out_3(budgetor_11_out_3));
  not not_14 (not_14_out, d_ff_2_q);
  not not_15 (not_15_out, d_ff_3_q);
  nand nand_4 (nand_4_out, not_10_out, not_13_out, not_11_out);
  not not_16 (not_16_out, nand_4_out);
  assign bit_extender_11_out = {{8{not_12_out}}, not_12_out};  // Bit_Extender bit_extender_11
  budgetOR budgetor_12 (.in_1(not_14_out), .in_2(not_15_out), .out_3(budgetor_12_out_3));
  not not_17 (not_17_out, rst_done);
  budgetOR budgetor_13 (.in_1(register_7_q), .in_2(not_16_out), .out_3(budgetor_13_out_3));
  not not_18 (not_18_out, budgetor_9_out_3);
  sixteen_to_9 sixteen_to_9_1 (.in_1(m_whole), .out_2(sixteen_to_9_1_out_2));
  assign bit_extender_12_out = {{3{not_12_out}}, not_12_out};  // Bit_Extender bit_extender_12
  Register #(.width(1)) register_7 (.D(budgetand_8_out_3), .en(not_18_out), .clk(CLK), .Q(register_7_q));  // open: clr
  budgetAND budgetand_8 (.in_1(not_17_out), .in_2(budgetor_13_out_3), .out_3(budgetand_8_out_3));
  assign nand_5_out = ~(bit_extender_11_out & sixteen_to_9_1_out_2);  // NAND_Gate nand_5, 9 bits wide
  assign nand_6_out = ~(bit_extender_12_out & m_frac);  // NAND_Gate nand_6, 4 bits wide
  assign not_19_out = ~nand_5_out;  // NOT_Gate not_19, 9 bits wide
  budgetAND budgetand_9 (.in_1(budgetor_10_out_3), .in_2(budgetor_12_out_3), .out_3(budgetand_9_out_3));
  assign not_20_out = ~nand_6_out;  // NOT_Gate not_20, 4 bits wide
  budgetAND budgetand_10 (.in_1(budgetor_11_out_3), .in_2(budgetor_12_out_3), .out_3(budgetand_10_out_3));
  Register #(.width(9)) ans_whole (.D(not_19_out), .en(budgetand_9_out_3), .clk(CLK), .Q(awh));  // open: clr
  Register #(.width(4)) ans_frac (.D(not_20_out), .en(budgetand_10_out_3), .clk(CLK), .Q(af));  // open: clr
  budgetAND budgetand_11 (.in_1(rdy), .in_2(register_7_q), .out_3(sel_lock));

  // Other names for the same wires on the sheet: DONE = eq

  // Notes on the sheet:
  //   insert values
  //   input queue
  //   load in values
  //   start
  //   add frac parts
  //   binary search stuff, with three variables, end, start, and middle(dw about it)
  //   add whole parts
  //   is our for loop done?
  //   is middle equal to the root of our number?
  //   delay output by 1 clock cycle for synconized results
  //   needs to be 9-bit
  //   stop end from modifying itself without my permission
  //   this is 4-bit precision for a reason
endmodule

module budgetAND (
  input  in_1,
  input  in_2,
  output out_3
);

  wire nand_1_out;

  nand nand_1 (nand_1_out, in_1, in_2);
  not not_1 (out_3, nand_1_out);
endmodule

module budgetOR (
  input  in_1,
  input  in_2,
  output out_3
);

  wire not_1_out, not_2_out;

  not not_1 (not_1_out, in_1);
  not not_2 (not_2_out, in_2);
  nand nand_1 (out_3, not_1_out, not_2_out);
endmodule

module div_by_2 (
  input  [16:0] in_1,
  input  [3:0] f,
  output [3:0] fout,
  output [15:0] out_4
);


  assign fout = {in_1[0], f[3:1]};
  assign out_4 = in_1[16:1];

  // Other names for the same wires on the sheet: frac[3:0] = f
endmodule

module bit_normalization (
  input  [8:0] in_1,
  input  [8:0] c_over,
  output [15:0] out_3
);


  assign out_3 = {c_over[6:0], in_1};
endmodule

module sixteen_to_17 (
  input  [15:0] in_1,
  input  in_2,
  output [16:0] out_3
);


  assign out_3 = {in_2, in_1};
endmodule

module m_square (
  input  [15:0] in_1,
  input  [3:0] f,
  output [3:0] frac,
  output [15:0] whole
);

  wire adder_1_cout;
  wire [3:0] multiplier_2_cout;
  wire [15:0] bit_extender_1_out, multiplier_1_out, multiplier_3_out;

  assign bit_extender_1_out = {{12{1'b0}}, f};  // Bit_Extender bit_extender_1
  Multiplier #(.width(16)) multiplier_1 (.a(in_1), .b(in_1), .out(multiplier_1_out));  // open: cin, cout
  Multiplier #(.width(4)) multiplier_2 (.a(f), .b(f), .cout(multiplier_2_cout));  // open: out, cin
  Multiplier #(.width(16)) multiplier_3 (.a(bit_extender_1_out), .b(in_1), .out(multiplier_3_out));  // open: cin, cout
  // Probe on {multiplier_3_out[2:0], 1'b0}
  // Probe on multiplier_2_cout
  Adder #(.width(4)) adder_1 (
    .a({multiplier_3_out[2:0], 1'b0}), .b(multiplier_2_cout), .out(frac), .cout(adder_1_cout));  // open: cin
  Adder #(.width(16)) adder_2 (
    .a({3'b000, multiplier_3_out[15:3]}), .b(multiplier_1_out), .out(whole), .cin(adder_1_cout));  // open: cout
  // Probe on whole
endmodule

module add_1 (
  input  [15:0] in_1,
  output [15:0] out_2
);

  Adder #(.width(16)) adder_1 (.a(in_1), .b(16'h1), .out(out_2));  // open: cin, cout
endmodule

module carry_over (
  input  [7:0] in_1,
  input  in_2,
  output [8:0] out_3
);


  assign out_3 = {in_2, in_1};
endmodule

module sq_controller (
  input  Q1,
  input  Q0,
  input  RST,
  input  eq,
  input  rdy,
  input  gt,
  output Q1n,
  output Q0n,
  output found
);

  wire nand_1_out, nand_2_out, nand_3_out, nand_4_out, nand_5_out, nand_6_out, not_1_out, not_2_out,
       not_3_out, not_4_out, not_5_out;

  not not_1 (not_1_out, eq);
  not not_2 (not_2_out, gt);
  not not_3 (not_3_out, Q1);
  not not_4 (not_4_out, Q0);
  nand nand_1 (nand_1_out, eq, Q0);
  nand nand_2 (nand_2_out, gt, Q0);
  nand nand_3 (nand_3_out, not_1_out, not_2_out, Q0);
  nand nand_4 (nand_4_out, rdy, not_3_out, not_4_out);
  nand nand_5 (nand_5_out, nand_1_out, nand_2_out);
  nand nand_6 (nand_6_out, nand_3_out, nand_4_out);
  not not_5 (not_5_out, RST);
  budgetAND budgetand_1 (.in_1(nand_5_out), .in_2(not_5_out), .out_3(Q1n));
  budgetAND budgetand_2 (.in_1(nand_6_out), .in_2(not_5_out), .out_3(Q0n));

  assign found = Q1;
endmodule

module sixteen_to_9 (
  input  [15:0] in_1,
  output [8:0] out_2
);


  assign out_2 = in_1[8:0];
endmodule

module input_extender (
  input  [7:0] in_1,
  output out_2
);


  assign out_2 = in_1[7];
endmodule

module accuracy_controller (
  input  Q1,
  input  Q0,
  input  RST,
  input  lt,
  input  rdy,
  output Q1n,
  output Q0n,
  output done
);

  wire nand_1_out, nand_2_out, nand_3_out, nand_4_out, not_1_out, not_2_out, not_3_out, not_4_out, not_5_out;

  not not_1 (not_1_out, lt);
  not not_2 (not_2_out, Q1);
  not not_3 (not_3_out, Q0);
  nand nand_1 (nand_1_out, not_1_out, Q0);
  nand nand_2 (nand_2_out, rdy, not_2_out, not_3_out);
  nand nand_3 (nand_3_out, lt, Q0);
  not not_4 (not_4_out, nand_1_out);
  nand nand_4 (nand_4_out, nand_2_out, nand_3_out);
  not not_5 (not_5_out, RST);
  budgetAND budgetand_1 (.in_1(not_4_out), .in_2(not_5_out), .out_3(Q1n));
  budgetAND budgetand_2 (.in_1(nand_4_out), .in_2(not_5_out), .out_3(Q0n));

  assign done = Q1;
endmodule

module the_precisioner (
  input  DONE,
  input  RST,
  input  eq,
  input  [8:0] awh,
  input  [3:0] af,
  input  [16:0] num,
  input  CLK,
  output [8:0] awhn,
  output [3:0] afn,
  output lt
);

  wire adder_2_cout, budgetand_1_out_3, budgetor_1_out_3, gt, not_1_out;
  wire [3:0] adder_1_out, bit_extender_1_out, nand_1_out, not_2_out, register_1_q;
  wire [8:0] bit_extender_2_out;
  wire [15:0] bit_extender_3_out, m_square_1_whole;
  wire [16:0] bit_extender_4_out;

  Adder #(.width(4)) adder_1 (.a(register_1_q), .b(4'b0001), .out(adder_1_out));  // open: cin, cout
  not not_1 (not_1_out, budgetor_1_out_3);
  budgetOR budgetor_1 (.in_1(DONE), .in_2(RST), .out_3(budgetor_1_out_3));
  assign bit_extender_1_out = {{3{not_1_out}}, not_1_out};  // Bit_Extender bit_extender_1
  budgetAND budgetand_1 (.in_1(gt), .in_2(eq), .out_3(budgetand_1_out_3));
  assign nand_1_out = ~(bit_extender_1_out & adder_1_out);  // NAND_Gate nand_1, 4 bits wide
  assign not_2_out = ~nand_1_out;  // NOT_Gate not_2, 4 bits wide
  Register #(.width(4)) register_1 (.D(not_2_out), .en(budgetand_1_out_3), .clk(CLK), .Q(register_1_q));  // open: clr
  Adder #(.width(4)) adder_2 (.a(register_1_q), .b(af), .out(afn), .cout(adder_2_cout));  // open: cin
  assign bit_extender_2_out = {{8{1'b0}}, adder_2_cout};  // Bit_Extender bit_extender_2
  Adder #(.width(9)) adder_3 (.a(bit_extender_2_out), .b(awh), .out(awhn));  // open: cin, cout
  assign bit_extender_3_out = {{7{1'b0}}, awhn};  // Bit_Extender bit_extender_3
  m_square m_square_1 (.in_1(bit_extender_3_out), .f(afn), .whole(m_square_1_whole));  // open: frac
  assign bit_extender_4_out = {{1{1'b0}}, m_square_1_whole};  // Bit_Extender bit_extender_4
  Comparator #(.mode("unsigned"), .width(17)) comparator_1 (.a(bit_extender_4_out), .b(num), .lt(gt));  // open: gt, eq
  not not_3 (lt, gt);
endmodule

module unifier (
  input  [3:0] in_1,
  input  [8:0] in_2,
  output [11:0] out_3
);


  assign out_3 = {in_2, in_1[3:1]};
endmodule

module test (
  input  [16:0] in_1,
  output [11:0] out_2
);

  wire subtractor_1_bout, subtractor_2_bout, subtractor_3_bout, subtractor_4_bout, subtractor_5_bout,
       subtractor_6_bout, subtractor_7_bout, subtractor_8_bout, subtractor_9_bout, subtractor_10_bout,
       subtractor_11_bout;
  wire [1:0] bit_extender_1_out, multiplexer_1_out;
  wire [2:0] bit_extender_2_out, bit_extender_3_out, multiplexer_2_out, subtractor_1_out;
  wire [3:0] bit_extender_4_out, bit_extender_5_out, multiplexer_3_out, subtractor_2_out;
  wire [4:0] bit_extender_6_out, bit_extender_7_out, multiplexer_4_out, subtractor_3_out;
  wire [5:0] bit_extender_8_out, bit_extender_9_out, subtractor_4_out;
  wire [6:0] bit_extender_10_out, bit_extender_11_out, multiplexer_6_out, subtractor_5_out;
  wire [7:0] bit_extender_12_out, bit_extender_13_out, multiplexer_7_out, subtractor_6_out;
  wire [7:2] multiplexer_5_out;
  wire [8:0] bit_extender_14_out, bit_extender_15_out, multiplexer_8_out, subtractor_7_out;
  wire [9:0] bit_extender_16_out, bit_extender_17_out, multiplexer_9_out, subtractor_8_out;
  wire [10:0] bit_extender_18_out, bit_extender_19_out, multiplexer_10_out, subtractor_9_out;
  wire [11:0] subtractor_10_out;
  wire [12:0] subtractor_11_out;

  not not_1 (out_2[10], subtractor_1_bout);
  not not_2 (out_2[9], subtractor_2_bout);
  Bit_Extender #(.in_width(3), .out_width(2), .\type ("zero")) bit_extender_1 (
    .in(subtractor_1_out), .out(bit_extender_1_out));
  Subtractor #(.width(3)) subtractor_1 (
    .a({1'b0, in_1[15:14]}), .b({in_1[16], 2'b01}), .out(subtractor_1_out), .bout(subtractor_1_bout));  // open: bin
  Multiplexer #(.width(2)) multiplexer_1 (
    .in0(in_1[15:14]), .in1(bit_extender_1_out), .out(multiplexer_1_out), .sel(out_2[10]));
  not not_3 (out_2[8], subtractor_3_bout);
  not not_4 (out_2[7], subtractor_4_bout);
  not not_5 (out_2[6], subtractor_5_bout);
  not not_6 (out_2[5], subtractor_6_bout);
  not not_7 (out_2[4], subtractor_7_bout);
  not not_8 (out_2[3], subtractor_8_bout);
  not not_9 (out_2[2], subtractor_9_bout);
  not not_10 (out_2[1], subtractor_10_bout);
  not not_11 (out_2[0], subtractor_11_bout);
  Subtractor #(.width(4)) subtractor_2 (
    .a({multiplexer_1_out, in_1[13:12]}), .b({in_1[16], out_2[10], 2'b01}), .out(subtractor_2_out),
    .bout(subtractor_2_bout));  // open: bin
  Bit_Extender #(.in_width(4), .out_width(3), .\type ("zero")) bit_extender_2 (
    .in({multiplexer_1_out, in_1[13:12]}), .out(bit_extender_2_out));
  Bit_Extender #(.in_width(4), .out_width(3), .\type ("zero")) bit_extender_3 (
    .in(subtractor_2_out), .out(bit_extender_3_out));
  Multiplexer #(.width(3)) multiplexer_2 (
    .in0(bit_extender_2_out), .in1(bit_extender_3_out), .out(multiplexer_2_out), .sel(out_2[9]));
  Subtractor #(.width(5)) subtractor_3 (
    .a({multiplexer_2_out, in_1[11:10]}), .b({in_1[16], out_2[10:9], 2'b01}), .out(subtractor_3_out),
    .bout(subtractor_3_bout));  // open: bin
  Bit_Extender #(.in_width(5), .out_width(4)) bit_extender_4 (
    .in({multiplexer_2_out, in_1[11:10]}), .out(bit_extender_4_out));
  Multiplexer #(.width(4)) multiplexer_3 (
    .in0(bit_extender_4_out), .in1(bit_extender_5_out), .out(multiplexer_3_out), .sel(out_2[8]));
  Bit_Extender #(.in_width(5), .out_width(4), .\type ("zero")) bit_extender_5 (
    .in(subtractor_3_out), .out(bit_extender_5_out));
  Bit_Extender #(.in_width(6), .out_width(5), .\type ("zero")) bit_extender_6 (
    .in(subtractor_4_out), .out(bit_extender_6_out));
  Subtractor #(.width(6)) subtractor_4 (
    .a({multiplexer_3_out, in_1[9:8]}), .b({in_1[16], out_2[10:8], 2'b01}), .out(subtractor_4_out),
    .bout(subtractor_4_bout));  // open: bin
  Bit_Extender #(.in_width(6), .out_width(5), .\type ("zero")) bit_extender_7 (
    .in({multiplexer_3_out, in_1[9:8]}), .out(bit_extender_7_out));
  Multiplexer #(.width(5)) multiplexer_4 (
    .in0(bit_extender_7_out), .in1(bit_extender_6_out), .out(multiplexer_4_out), .sel(out_2[7]));
  Subtractor #(.width(7)) subtractor_5 (
    .a({multiplexer_4_out, in_1[7:6]}), .b({in_1[16], out_2[10:7], 2'b01}), .out(subtractor_5_out),
    .bout(subtractor_5_bout));  // open: bin
  Bit_Extender #(.in_width(7), .out_width(6), .\type ("zero")) bit_extender_8 (
    .in({multiplexer_4_out, in_1[7:6]}), .out(bit_extender_8_out));
  Multiplexer #(.width(6)) multiplexer_5 (
    .in0(bit_extender_8_out), .in1(bit_extender_9_out), .out(multiplexer_5_out), .sel(out_2[6]));
  Bit_Extender #(.in_width(7), .out_width(6), .\type ("zero")) bit_extender_9 (
    .in(subtractor_5_out), .out(bit_extender_9_out));
  Bit_Extender #(.out_width(7), .\type ("zero")) bit_extender_10 (.in(subtractor_6_out), .out(bit_extender_10_out));
  Subtractor subtractor_6 (
    .a({multiplexer_5_out, in_1[5:4]}), .b({in_1[16], out_2[10:6], 2'b01}), .out(subtractor_6_out),
    .bout(subtractor_6_bout));  // open: bin
  Bit_Extender #(.out_width(7), .\type ("zero")) bit_extender_11 (
    .in({multiplexer_5_out, in_1[5:4]}), .out(bit_extender_11_out));
  Multiplexer #(.width(7)) multiplexer_6 (
    .in0(bit_extender_11_out), .in1(bit_extender_10_out), .out(multiplexer_6_out), .sel(out_2[5]));
  Bit_Extender #(.in_width(9), .out_width(8), .\type ("zero")) bit_extender_12 (
    .in(subtractor_7_out), .out(bit_extender_12_out));
  Subtractor #(.width(9)) subtractor_7 (
    .a({multiplexer_6_out, in_1[3:2]}), .b({in_1[16], out_2[10:5], 2'b01}), .out(subtractor_7_out),
    .bout(subtractor_7_bout));  // open: bin
  Bit_Extender #(.in_width(9), .out_width(8), .\type ("zero")) bit_extender_13 (
    .in({multiplexer_6_out, in_1[3:2]}), .out(bit_extender_13_out));
  Multiplexer #(.width(8)) multiplexer_7 (
    .in0(bit_extender_13_out), .in1(bit_extender_12_out), .out(multiplexer_7_out), .sel(out_2[4]));
  Subtractor #(.width(10)) subtractor_8 (
    .a({multiplexer_7_out, in_1[1:0]}), .b({in_1[16], out_2[10:4], 2'b01}), .out(subtractor_8_out),
    .bout(subtractor_8_bout));  // open: bin
  Bit_Extender #(.in_width(10), .out_width(9), .\type ("zero")) bit_extender_14 (
    .in({multiplexer_7_out, in_1[1:0]}), .out(bit_extender_14_out));
  Multiplexer #(.width(9)) multiplexer_8 (
    .in0(bit_extender_14_out), .in1(bit_extender_15_out), .out(multiplexer_8_out), .sel(out_2[3]));
  Bit_Extender #(.in_width(10), .out_width(9), .\type ("zero")) bit_extender_15 (
    .in(subtractor_8_out), .out(bit_extender_15_out));
  Bit_Extender #(.in_width(11), .out_width(10), .\type ("zero")) bit_extender_16 (
    .in(subtractor_9_out), .out(bit_extender_16_out));
  Subtractor #(.width(11)) subtractor_9 (
    .a({multiplexer_8_out, 2'b00}), .b({in_1[16], out_2[10:3], 2'b01}), .out(subtractor_9_out),
    .bout(subtractor_9_bout));  // open: bin
  Bit_Extender #(.in_width(11), .out_width(10), .\type ("zero")) bit_extender_17 (
    .in({multiplexer_8_out, 2'b00}), .out(bit_extender_17_out));
  Multiplexer #(.width(10)) multiplexer_9 (
    .in0(bit_extender_17_out), .in1(bit_extender_16_out), .out(multiplexer_9_out), .sel(out_2[2]));
  Bit_Extender #(.in_width(12), .out_width(11), .\type ("zero")) bit_extender_18 (
    .in(subtractor_10_out), .out(bit_extender_18_out));
  Subtractor #(.width(12)) subtractor_10 (
    .a({multiplexer_9_out, 2'b00}), .b({in_1[16], out_2[10:2], 2'b01}), .out(subtractor_10_out),
    .bout(subtractor_10_bout));  // open: bin
  Bit_Extender #(.in_width(12), .out_width(11), .\type ("zero")) bit_extender_19 (
    .in({multiplexer_9_out, 2'b00}), .out(bit_extender_19_out));
  Multiplexer #(.width(11)) multiplexer_10 (
    .in0(bit_extender_19_out), .in1(bit_extender_18_out), .out(multiplexer_10_out), .sel(out_2[1]));
  Subtractor #(.width(13)) subtractor_11 (
    .a({multiplexer_10_out, 2'b00}), .b({in_1[16], out_2[10:1], 2'b01}), .out(subtractor_11_out),
    .bout(subtractor_11_bout));  // open: bin
  Bit_Extender #(.in_width(13), .out_width(12), .\type ("zero")) bit_extender_20 (.in(subtractor_11_out));  // open: out

  assign out_2[11] = in_1[16];

  // Other names for the same wires on the sheet: BG2[1:0] = in_1[13:12]; BG3[1:0] = in_1[11:10]; BG4[1:0] = in_1[9:8];
  //   BG5[1:0] = in_1[7:6]; BG6[1:0] = in_1[5:4]; BG7[1:0] = in_1[3:2]; BG8[1:0] = in_1[1:0]; D0 = out_2[0];
  //   D1 = out_2[1]; D2 = out_2[2]; Q0 = out_2[3]; Q1 = out_2[4]; Q2 = out_2[5]; Q3 = out_2[6]; Q4 = out_2[7];
  //   Q5 = out_2[8]; Q6 = out_2[9]; Q7 = out_2[10]; Q8 = in_1[16]

  // Notes on the sheet:
  //   BG - bit group, grouping the bits into pairs to use non-restoring square root algorithm
  //   non-restoring square root algo: use subtraction and shifts to find each bit of the root of input
  //   actual number
  //   output:
  //   three decimal points of accuracy
endmodule

module test2 (
  input  [16:0] in_1
);


  // Notes on the sheet:
  //   actual number
  //   three decimal points of accuracy
endmodule

module minus_and_multiply (
  input  x,
  input  y,
  input  b,
  input  u,
  output bo,
  output d
);

  wire and_3_input_1_out_4, and_3_input_2_out_4, and_3_input_3_out_4, and_3_input_4_out_4,
       and_3_input_5_out_4, not_1_out, not_2_out, not_3_out, or_4_input_2_out_5;

  not not_1 (not_1_out, x);
  and_3_input and_3_input_1 (.in_1(b), .in_2(not_2_out), .in_3(not_1_out), .out_4(and_3_input_1_out_4));
  or_4_input or_4_input_1 (
    .in_1(and_3_input_4_out_4), .in_2(and_3_input_3_out_4), .in_3(and_3_input_2_out_4),
    .in_4(and_3_input_1_out_4), .out_5(bo));
  not not_2 (not_2_out, y);
  and_3_input and_3_input_2 (.in_1(not_3_out), .in_2(y), .in_3(not_1_out), .out_4(and_3_input_2_out_4));
  and_3_input and_3_input_3 (.in_1(b), .in_2(y), .in_3(not_1_out), .out_4(and_3_input_3_out_4));
  and_3_input and_3_input_4 (.in_1(b), .in_2(y), .in_3(x), .out_4(and_3_input_4_out_4));
  or_4_input or_4_input_2 (
    .in_1(and_3_input_5_out_4), .in_2(and_3_input_4_out_4), .in_3(and_3_input_2_out_4),
    .in_4(and_3_input_1_out_4), .out_5(or_4_input_2_out_5));
  Multiplexer multiplexer_1 (.in0(or_4_input_2_out_5), .in1(x), .out(d), .sel(u));
  not not_3 (not_3_out, b);
  and_3_input and_3_input_5 (.in_1(not_3_out), .in_2(not_2_out), .in_3(x), .out_4(and_3_input_5_out_4));
endmodule

module and_3_input (
  input  in_1,
  input  in_2,
  input  in_3,
  output out_4
);

  wire nand_1_out;

  nand nand_1 (nand_1_out, in_1, in_2, in_3);
  not not_1 (out_4, nand_1_out);
endmodule

module or_4_input (
  input  in_1,
  input  in_2,
  input  in_3,
  input  in_4,
  output out_5
);

  wire nand_1_out, nand_2_out, nand_3_out, nand_4_out;

  nand nand_1 (nand_1_out, in_1, in_1);
  nand nand_2 (nand_2_out, in_2, in_2);
  nand nand_3 (nand_3_out, in_3, in_3);
  nand nand_4 (nand_4_out, in_4, in_4);
  nand nand_5 (out_5, nand_1_out, nand_2_out, nand_3_out, nand_4_out);
endmodule
