// Logisim project backup.circ as structural Verilog
module DUT (
  input  X,
  input  CLK,
  input  RST,
  output Z
);

  wire nQ0, nQ1, nQ2, Q0, Q1, Q2, t0n_rst_1_out_9, t1n_rst_1_out_9, t2n_rst_1_out_9;

  output_func output_func_1 (.nQ2(nQ2), .nQ1(nQ1), .Q0(Q0), .out_4(Z));
  T_Flip_Flop T2 (.T(t2n_rst_1_out_9), .clk(CLK), .Q(Q2), .Qn(nQ2));  // open: reset, preset
  t2n_rst t2n_rst_1 (
    .x(X), .Q2(Q2), .nQ2(nQ2), .Q1(Q1), .nQ1(nQ1), .Q0(Q0), .nQ0(nQ0), .rst(RST), .out_9(t2n_rst_1_out_9));
  T_Flip_Flop T1 (.T(t1n_rst_1_out_9), .clk(CLK), .Q(Q1), .Qn(nQ1));  // open: reset, preset
  t1n_rst t1n_rst_1 (
    .x(X), .Q2(Q2), .nQ2(nQ2), .Q1(Q1), .nQ1(nQ1), .Q0(Q0), .nQ0(nQ0), .rst(RST), .out_9(t1n_rst_1_out_9));
  T_Flip_Flop T0 (.T(t0n_rst_1_out_9), .clk(CLK), .Q(Q0), .Qn(nQ0));  // open: reset, preset
  t0n_rst t0n_rst_1 (
    .x(X), .Q2(Q2), .nQ2(nQ2), .Q1(Q1), .nQ1(nQ1), .Q0(Q0), .nQ0(nQ0), .rst(RST), .out_9(t0n_rst_1_out_9));

  // Other names for the same wires on the sheet: z_out = Z

  // Notes on the sheet:
  //   Please put your deisgn below. You may also use subcircuits.
  //   However, do not move, rename, add, or delete any pins.
  //   Put your design below and wire it up to the pins.
  //   Feel free to remove this text.
endmodule

module TB (
);

  wire clk_out, mypor_1_p2, not_1_out, or_1_out, RESET_out, TimeIndex_carry, undriven;
  wire [0:0] dut_1_z;
  wire [4:0] TimeIndex_q;

  Clock #(.highDuration(2), .lowDuration(2)) clk (.out(clk_out));
  Clock sysclk ();  // open: out
  Counter #(.max('h1f), .ongoal("stay"), .width(5)) TimeIndex (
    .load(or_1_out), .clk(clk_out), .D({5{1'b0}}), .carry(TimeIndex_carry), .Q(TimeIndex_q));  // open: clr, up, count
  // MyPOR mypor_1: pin names not known; wires that end beside it: clk_out, mypor_1_p2
  Button RESET (.out(RESET_out));
  ROM #(.addrWidth(5), .dataWidth(1)) TestTraceMemory (.addr(TimeIndex_q));  // open: data
  or or_1 (or_1_out, mypor_1_p2, RESET_out);
  not not_1 (not_1_out, TimeIndex_carry);
  DUT dut_1 (.X(undriven), .CLK(clk_out), .RST(or_1_out), .Z(dut_1_z[0]));
  TTY tty_1 (.data({6'b011000, dut_1_z[0]}), .clk(clk_out), .we(not_1_out), .clr(or_1_out));
  LED DONE (.in(TimeIndex_carry));

  // Notes on the sheet:
  //   DO NOT MODIFY THIS
  //   YOU MAY TEST YOUR CIRCUITS USING THIS TO MAKE SURE YOU HAVE NOT ALTERED PIN OUT
  //   Edit ROM with input trace of 32 bits
  //   contents of TestTraceMemory (hex, n*v repeats v):
  //   1 1 1 0 1 0 0 0 1 1
endmodule

module TBRANDOM (
);

  wire clk_out, mypor_1_p2, not_1_out, or_1_out, random_1_out, RESET_out, TimeIndex_carry;
  wire [0:0] dut_1_z;

  Clock #(.highDuration(2), .lowDuration(2)) clk (.out(clk_out));
  Clock sysclk ();  // open: out
  Counter #(.ongoal("stay")) TimeIndex (
    .load(or_1_out), .clk(clk_out), .D({8{1'b0}}), .carry(TimeIndex_carry));  // open: clr, up, count, Q
  // MyPOR mypor_1: pin names not known; wires that end beside it: clk_out, mypor_1_p2
  Button RESET (.out(RESET_out));
  or or_1 (or_1_out, mypor_1_p2, RESET_out);
  Random #(.width(1)) random_1 (.clr(or_1_out), .clk(clk_out), .out(random_1_out));  // open: next
  not not_1 (not_1_out, TimeIndex_carry);
  DUT dut_1 (.X(random_1_out), .CLK(clk_out), .RST(or_1_out), .Z(dut_1_z[0]));
  TTY tty_1 (.data({6'b011000, dut_1_z[0]}), .clk(clk_out), .we(not_1_out), .clr(or_1_out));
  LED DONE (.in(TimeIndex_carry));

  // Notes on the sheet:
  //   DO NOT MODIFY THIS
  //   YOU MAY TEST YOUR CIRCUITS USING THIS TO MAKE SURE YOU HAVE NOT ALTERED PIN OUT
endmodule

module budgetAND (
  input  in_1,
  input  in_2,
  output out_3
);

  wire nand_1_out;

  nand nand_1 (nand_1_out, in_1, in_2);
  nand nand_2 (out_3, nand_1_out, nand_1_out);
endmodule

module budgetOR (
  input  in_1,
  input  in_2,
  output out_3
);

  wire nand_1_out, nand_2_out;

  nand nand_1 (nand_1_out, in_1, in_1);
  nand nand_2 (nand_2_out, in_2, in_2);
  nand nand_3 (out_3, nand_1_out, nand_2_out);
endmodule

module AND_3_input (
  input  in_1,
  input  in_2,
  input  in_3,
  output out_4
);

  wire budgetand_1_out_3;

  budgetAND budgetand_1 (.in_1(in_1), .in_2(in_2), .out_3(budgetand_1_out_3));
  budgetAND budgetand_2 (.in_1(budgetand_1_out_3), .in_2(in_3), .out_3(out_4));
endmodule

module OR_3_input (
  input  in_1,
  input  in_2,
  input  in_3,
  output out_4
);

  wire budgetor_1_out_3;

  budgetOR budgetor_1 (.in_1(in_1), .in_2(in_2), .out_3(budgetor_1_out_3));
  budgetOR budgetor_2 (.in_1(budgetor_1_out_3), .in_2(in_3), .out_3(out_4));
endmodule

module AND_4_input (
  input  in_1,
  input  in_2,
  input  in_3,
  input  in_4,
  output out_5
);

  wire budgetand_1_out_3, budgetand_2_out_3;

  budgetAND budgetand_1 (.in_1(in_1), .in_2(in_2), .out_3(budgetand_1_out_3));
  budgetAND budgetand_2 (.in_1(in_3), .in_2(in_4), .out_3(budgetand_2_out_3));
  budgetAND budgetand_3 (.in_1(budgetand_1_out_3), .in_2(budgetand_2_out_3), .out_3(out_5));
endmodule

module OR_4_input (
  input  in_1,
  input  in_2,
  input  in_3,
  input  in_4,
  output out_5
);

  wire budgetor_1_out_3, budgetor_2_out_3;

  budgetOR budgetor_1 (.in_1(in_1), .in_2(in_2), .out_3(budgetor_1_out_3));
  budgetOR budgetor_2 (.in_1(in_3), .in_2(in_4), .out_3(budgetor_2_out_3));
  budgetOR budgetor_3 (.in_1(budgetor_1_out_3), .in_2(budgetor_2_out_3), .out_3(out_5));
endmodule

module output_func (
  input  nQ2,
  input  nQ1,
  input  Q0,
  output out_4
);

  AND_3_input and_3_input_1 (.in_1(nQ2), .in_2(nQ1), .in_3(Q0), .out_4(out_4));
endmodule

module t2n_rst (
  input  x,
  input  Q2,
  input  nQ2,
  input  Q1,
  input  nQ1,
  input  Q0,
  input  nQ0,
  input  rst,
  output out_9
);

  wire budgetand_1_out_3, budgetand_2_out_3, budgetand_3_out_3, or_3_input_1_out_4;

  budgetAND budgetand_1 (.in_1(Q2), .in_2(Q0), .out_3(budgetand_1_out_3));
  budgetAND budgetand_2 (.in_1(nQ2), .in_2(nQ0), .out_3(budgetand_2_out_3));
  OR_3_input or_3_input_1 (.in_1(x), .in_2(budgetand_1_out_3), .in_3(budgetand_2_out_3), .out_4(or_3_input_1_out_4));
  budgetAND budgetand_3 (.in_1(or_3_input_1_out_4), .in_2(Q1), .out_3(budgetand_3_out_3));
  mux_2 mux_2_1 (.in_1(budgetand_3_out_3), .in_2(Q2), .in_3(rst), .out_4(out_9));
endmodule

module t1n_rst (
  input  x,
  input  Q2,
  input  nQ2,
  input  Q1,
  input  nQ1,
  input  Q0,
  input  nQ0,
  input  rst,
  output out_9
);

  wire and_3_input_1_out_4, budgetor_1_out_3, budgetor_2_out_3, or_3_input_1_out_4;

  budgetOR budgetor_1 (.in_1(x), .in_2(Q2), .out_3(budgetor_1_out_3));
  OR_3_input or_3_input_1 (.in_1(nQ2), .in_2(Q1), .in_3(Q0), .out_4(or_3_input_1_out_4));
  budgetOR budgetor_2 (.in_1(nQ1), .in_2(nQ0), .out_3(budgetor_2_out_3));
  AND_3_input and_3_input_1 (
    .in_1(budgetor_1_out_3), .in_2(or_3_input_1_out_4), .in_3(budgetor_2_out_3), .out_4(and_3_input_1_out_4));
  mux_2 mux_2_1 (.in_1(and_3_input_1_out_4), .in_2(Q1), .in_3(rst), .out_4(out_9));
endmodule

module t0n_rst (
  input  x,
  input  Q2,
  input  nQ2,
  input  Q1,
  input  nQ1,
  input  Q0,
  input  nQ0,
  input  rst,
  output out_9
);

  wire and_3_input_1_out_4, not_1_out, or_3_input_1_out_4, or_3_input_2_out_4, or_3_input_3_out_4;

  not not_1 (not_1_out, x);
  OR_3_input or_3_input_1 (.in_1(not_1_out), .in_2(nQ2), .in_3(Q1), .out_4(or_3_input_1_out_4));
  OR_3_input or_3_input_2 (.in_1(x), .in_2(nQ2), .in_3(nQ1), .out_4(or_3_input_2_out_4));
  OR_3_input or_3_input_3 (.in_1(Q2), .in_2(Q1), .in_3(nQ0), .out_4(or_3_input_3_out_4));
  AND_3_input and_3_input_1 (
    .in_1(or_3_input_1_out_4), .in_2(or_3_input_2_out_4), .in_3(or_3_input_3_out_4),
    .out_4(and_3_input_1_out_4));
  mux_2 mux_2_1 (.in_1(and_3_input_1_out_4), .in_2(Q0), .in_3(rst), .out_4(out_9));
endmodule

module mux_2 (
  input  in_1,
  input  in_2,
  input  in_3,
  output out_4
);

  wire budgetand_1_out_3, budgetand_2_out_3, not_1_out;

  not not_1 (not_1_out, in_3);
  budgetAND budgetand_1 (.in_1(in_1), .in_2(not_1_out), .out_3(budgetand_1_out_3));
  budgetAND budgetand_2 (.in_1(in_2), .in_2(in_3), .out_3(budgetand_2_out_3));
  budgetOR budgetor_1 (.in_1(budgetand_1_out_3), .in_2(budgetand_2_out_3), .out_3(out_4));
endmodule
