// Logisim project da1_task1.circ as structural Verilog: 13 circuits, main circuit DUT
module DUT (
  input  [15:0] A,
  input  [15:0] B,
  output [15:0] DOUT,
  output AWON
);

  wire comparator_1_eq, comparator_1_gt;
  wire [4:0] one_adder_1_out_2, one_adder_2_out_2;

  // Probe on one_adder_2_out_2
  one_adder one_adder_1 (.in_1(A), .out_2(one_adder_1_out_2));
  one_adder one_adder_2 (.in_1(B), .out_2(one_adder_2_out_2));
  // Probe on one_adder_1_out_2
  // Probe on DOUT
  Multiplexer #(.width(16)) multiplexer_1 (.in0(B), .in1(A), .out(DOUT), .sel(AWON));
  Comparator #(.mode("unsigned"), .width(5)) comparator_1 (
    .a(one_adder_1_out_2), .b(one_adder_2_out_2), .gt(comparator_1_gt), .eq(comparator_1_eq));  // open: lt
  budgetOR budgetor_1 (.in_1(comparator_1_gt), .in_2(comparator_1_eq), .out_3(AWON));

  // Other names for the same wires on the sheet: a_d[15:0] = A; b_d[15:0] = B

  // Notes on the sheet:
  //   Please put your deisgn below. You may also use subcircuits.
  //   However, do not move or rename any pins.
endmodule

module TB (
  input  [15:0] A,
  input  [15:0] B,
  output [15:0] DOUT,
  output AWON
);

  DUT dut_1 (.A(A), .B(B), .DOUT(DOUT), .AWON(AWON));

  // Notes on the sheet:
  //   DO NOT MODIFY THIS
  //   TEST YOUR CIRCUITS USING THIS TO MAKE SURE YOU HAVE NOT ALTERED PIN OUT
endmodule

module budgetAND (
  input  A,
  input  B,
  output out_3
);

  wire nand_1_out;

  nand nand_1 (nand_1_out, A, B);
  nand nand_2 (out_3, nand_1_out, nand_1_out);
endmodule

module one_adder (
  input  [15:0] in_1,
  output [4:0] out_2
);

  wire adder_1_cout, adder_1_out, adder_2_cout, adder_2_out, adder_3_cout, adder_3_out, adder_4_cout,
       adder_4_out, adder_5_cout, adder_5_out, adder_6_cout, adder_6_out, adder_7_cout, adder_7_out,
       adder_8_cout, adder_8_out, adder_9_cout, adder_9_out, adder_10_cout, adder_10_out, adder_11_cout,
       adder_11_out, half_adder_1_c, half_adder_2_c, half_adder_3_c;

  Adder #(.width(1)) adder_1 (.a(in_1[2]), .b(in_1[3]), .out(adder_1_out), .cin(in_1[1]), .cout(adder_1_cout));
  Adder #(.width(1)) adder_2 (.a(in_1[5]), .b(in_1[6]), .out(adder_2_out), .cin(in_1[4]), .cout(adder_2_cout));
  Adder #(.width(1)) adder_3 (.a(in_1[8]), .b(in_1[9]), .out(adder_3_out), .cin(in_1[7]), .cout(adder_3_cout));
  Adder #(.width(1)) adder_4 (.a(in_1[11]), .b(in_1[12]), .out(adder_4_out), .cin(in_1[10]), .cout(adder_4_cout));
  Adder #(.width(1)) adder_5 (.a(in_1[14]), .b(in_1[15]), .out(adder_5_out), .cin(in_1[13]), .cout(adder_5_cout));
  Adder #(.width(1)) adder_6 (.a(adder_1_out), .b(adder_2_out), .out(adder_6_out), .cin(in_1[0]), .cout(adder_6_cout));
  Adder #(.width(1)) adder_7 (
    .a(adder_2_cout), .b(adder_3_cout), .out(adder_7_out), .cin(adder_6_cout), .cout(adder_7_cout));
  Adder #(.width(1)) adder_8 (
    .a(adder_4_out), .b(adder_5_out), .out(adder_8_out), .cin(adder_3_out), .cout(adder_8_cout));
  Adder #(.width(1)) adder_9 (
    .a(adder_4_cout), .b(adder_5_cout), .out(adder_9_out), .cin(adder_8_cout), .cout(adder_9_cout));
  Adder #(.width(1)) adder_10 (
    .a(adder_7_out), .b(adder_9_out), .out(adder_10_out), .cin(adder_1_cout), .cout(adder_10_cout));
  half_adder half_adder_1 (.in_1(adder_6_out), .in_2(adder_8_out), .out_3(out_2[0]), .c(half_adder_1_c));
  Adder #(.width(1)) adder_11 (
    .a(adder_10_cout), .b(adder_9_cout), .out(adder_11_out), .cin(adder_7_cout), .cout(adder_11_cout));
  half_adder half_adder_2 (.in_1(half_adder_1_c), .in_2(adder_10_out), .out_3(out_2[1]), .c(half_adder_2_c));
  half_adder half_adder_3 (.in_1(half_adder_2_c), .in_2(adder_11_out), .out_3(out_2[2]), .c(half_adder_3_c));
  half_adder half_adder_4 (.in_1(half_adder_3_c), .in_2(adder_11_cout), .out_3(out_2[3]), .c(out_2[4]));
  // Probe on out_2

  // Notes on the sheet:
  //   Outputs sum of 1's in input as a binary value
endmodule

module budgetOR (
  input  in_1,
  input  in_2,
  output out_3
);

  wire nand_1_out, nand_2_out;

  nand nand_1 (nand_1_out, in_1, in_1);
  nand nand_2 (nand_2_out, in_2, in_2);
  nand nand_3 (out_3, nand_1_out, nand_2_out);
endmodule

module budgetNOR (
  input  in_1,
  input  in_2,
  output out_3
);

  wire budgetor_1_out_3;

  not not_1 (out_3, budgetor_1_out_3);
  budgetOR budgetor_1 (.in_1(in_1), .in_2(in_2), .out_3(budgetor_1_out_3));
endmodule

module budgetXOR (
  input  in_1,
  input  in_2,
  output out_3
);

  wire nand_1_out, nand_2_out, nand_3_out;

  nand nand_1 (nand_1_out, in_1, in_2);
  nand nand_2 (nand_2_out, in_1, nand_1_out);
  nand nand_3 (nand_3_out, nand_1_out, in_2);
  nand nand_4 (out_3, nand_2_out, nand_3_out);
endmodule

module budgetXNOR (
  input  in_1,
  input  in_2,
  output out_3
);

  wire budgetxor_1_out_3;

  budgetXOR budgetxor_1 (.in_1(in_1), .in_2(in_2), .out_3(budgetxor_1_out_3));
  not not_1 (out_3, budgetxor_1_out_3);
endmodule

module three_to_4 (
  input  [2:0] in_1,
  input  Cin,
  output [3:0] out_3
);

  // Probe on {Cin, in_1}

  assign out_3 = {Cin, in_1};
endmodule

module four_to_5 (
  input  [3:0] in_1,
  input  Cin,
  output [4:0] out_3
);

  // Probe on {Cin, in_1}

  assign out_3 = {Cin, in_1};
endmodule

module one_to_2 (
  input  in_1,
  input  Cin,
  output [1:0] out_3
);


  assign out_3 = {Cin, in_1};
endmodule

module two_to_3 (
  input  [1:0] in_1,
  input  Cin,
  output [2:0] out_3
);

  // Probe on {Cin, in_1}

  assign out_3 = {Cin, in_1};
endmodule

module half_adder (
  input  in_1,
  input  in_2,
  output out_3,
  output c
);

  budgetXOR budgetxor_1 (.in_1(in_1), .in_2(in_2), .out_3(out_3));
  budgetAND budgetand_1 (.A(in_1), .B(in_2), .out_3(c));
endmodule
