// Logisim project da1_task2.circ as structural Verilog: 11 circuits, main circuit DUT
module DUT (
  input  [6:0] SIGN,
  input  [6:0] D1,
  input  [6:0] D0,
  output [7:0] TC,
  output NAN
);

  wire p_n, sign_and_dig_check_1_out_4;
  wire [0:0] not_1_out;
  wire [3:0] dig0, dig1;
  wire [6:0] conv_digits_1_out_3;
  wire [7:0] adder_1_out, multiplexer_1_out, not_2_out;

  pos_or_neg pos_or_neg_1 (.a(SIGN), .z(p_n));
  // Probe on SIGN
  into_number into_number_1 (.a(D1), .x(dig1));
  into_number into_number_2 (.a(D0), .x(dig0));
  sign_and_dig_check sign_and_dig_check_1 (.SIGN(SIGN), .D1(D1), .D0(D0), .out_4(sign_and_dig_check_1_out_4));
  not not_1 (not_1_out[0], p_n);
  assign not_2_out = ~{1'b0, conv_digits_1_out_3};  // NOT_Gate not_2, 8 bits wide
  conv_digits conv_digits_1 (.in_1(dig1), .in_2(dig0), .out_3(conv_digits_1_out_3));
  Adder adder_1 (.a({{7{1'b0}}, not_1_out[0]}), .b(multiplexer_1_out), .out(adder_1_out));  // open: cin, cout
  Multiplexer #(.width(8)) multiplexer_1 (
    .in0(not_2_out), .in1({1'b0, conv_digits_1_out_3}), .out(multiplexer_1_out), .sel(p_n));
  Multiplexer #(.width(8)) multiplexer_2 (
    .in0({8{1'b1}}), .in1(adder_1_out), .out(TC), .sel(sign_and_dig_check_1_out_4));
  // Probe on adder_1_out
  not not_3 (NAN, sign_and_dig_check_1_out_4);

  // Notes on the sheet:
  //   Please put your deisgn below. You may also use subcircuits.
  //   However, do not move or rename any pins.
  //   pos sign
endmodule

module TB (
  input  [6:0] SIGN,
  input  [6:0] D1,
  input  [6:0] D0,
  output [7:0] DOUT,
  output NAN
);

  DUT dut_1 (.SIGN(SIGN), .D1(D1), .D0(D0), .TC(DOUT), .NAN(NAN));

  // Notes on the sheet:
  //   DO NOT MODIFY THIS
  //   TEST YOUR CIRCUITS USING THIS TO MAKE SURE YOU HAVE NOT ALTERED PIN OUT
endmodule

module sign_and_dig_check (
  input  [6:0] SIGN,
  input  [6:0] D1,
  input  [6:0] D0,
  output out_4
);

  wire budgetand_1_out_3, budgetand_2_out_3, budgetand_3_out_3, budgetand_4_out_3, budgetand_5_out_3,
       budgetand_6_out_3, budgetand_7_out_3, budgetxnor_1_out_3, budgetxnor_2_out_3, comparator_1_gt,
       comparator_2_gt, comparator_3_eq, not_1_out, pos_or_neg_1_z;
  wire [6:0] multiplexer_1_out;

  pos_or_neg pos_or_neg_1 (.a(SIGN), .z(pos_or_neg_1_z));
  Multiplexer #(.width(7)) multiplexer_1 (.in0(7'b0101011), .in1(7'b0101101), .out(multiplexer_1_out), .sel(not_1_out));
  not not_1 (not_1_out, pos_or_neg_1_z);
  Comparator #(.mode("unsigned"), .width(4)) comparator_1 (
    .a(4'b1010), .b(D1[3:0]), .gt(comparator_1_gt));  // open: eq, lt
  budgetAND budgetand_1 (.in_1(D1[4]), .in_2(D1[5]), .out_3(budgetand_1_out_3));
  budgetXNOR budgetxnor_1 (.in_1(D1[6]), .in_2(1'b0), .out_3(budgetxnor_1_out_3));
  Comparator #(.mode("unsigned"), .width(4)) comparator_2 (
    .a(4'b1010), .b(D0[3:0]), .gt(comparator_2_gt));  // open: eq, lt
  budgetAND budgetand_2 (.in_1(D0[4]), .in_2(D0[5]), .out_3(budgetand_2_out_3));
  budgetXNOR budgetxnor_2 (.in_1(D0[6]), .in_2(1'b0), .out_3(budgetxnor_2_out_3));
  Comparator #(.mode("unsigned"), .width(7)) comparator_3 (
    .a(SIGN), .b(multiplexer_1_out), .eq(comparator_3_eq));  // open: gt, lt
  budgetAND budgetand_3 (.in_1(comparator_1_gt), .in_2(budgetand_1_out_3), .out_3(budgetand_3_out_3));
  budgetAND budgetand_4 (.in_1(comparator_2_gt), .in_2(budgetand_2_out_3), .out_3(budgetand_4_out_3));
  budgetAND budgetand_5 (.in_1(budgetand_3_out_3), .in_2(budgetxnor_1_out_3), .out_3(budgetand_5_out_3));
  budgetAND budgetand_6 (.in_1(budgetand_4_out_3), .in_2(budgetxnor_2_out_3), .out_3(budgetand_6_out_3));
  budgetAND budgetand_7 (.in_1(comparator_3_eq), .in_2(budgetand_5_out_3), .out_3(budgetand_7_out_3));
  budgetAND budgetand_8 (.in_1(budgetand_7_out_3), .in_2(budgetand_6_out_3), .out_3(out_4));

  // Notes on the sheet:
  //   Sign bit has to be equal to either + or - in ASCII, check with equality comparator
  //   Digit has to be in range 0-9, checked with magnitude comparator
endmodule

module budgetAND (
  input  in_1,
  input  in_2,
  output out_3
);

  wire nand_1_out;

  nand nand_1 (nand_1_out, in_1, in_2);
  not not_1 (out_3, nand_1_out);
endmodule

module budgetXOR (
  input  in_1,
  input  in_2,
  output out_3
);

  wire nand_1_out, nand_2_out, nand_3_out;

  nand nand_1 (nand_1_out, in_1, in_2);
  nand nand_2 (nand_2_out, in_1, nand_1_out);
  nand nand_3 (nand_3_out, nand_1_out, in_2);
  nand nand_4 (out_3, nand_2_out, nand_3_out);
endmodule

module budgetXNOR (
  input  in_1,
  input  in_2,
  output out_3
);

  wire budgetxor_1_out_3;

  budgetXOR budgetxor_1 (.in_1(in_1), .in_2(in_2), .out_3(budgetxor_1_out_3));
  not not_1 (out_3, budgetxor_1_out_3);
endmodule

module budgetOR (
  input  in_1,
  input  in_2,
  output out_3
);

  wire not_1_out, not_2_out;

  not not_1 (not_1_out, in_1);
  not not_2 (not_2_out, in_2);
  nand nand_1 (out_3, not_1_out, not_2_out);
endmodule

module into_number (
  input  [6:0] a,
  output [3:0] x
);

  // Probe on a[3:0]

  assign x = a[3:0];

  // Notes on the sheet:
  //   translate 7-bit ASCII binary into normal binary digit
endmodule

module pos_or_neg (
  input  [6:0] a,
  output z
);

  not not_1 (z, a[2]);

  // Notes on the sheet:
  //   0 if neg sign, 1 if pos sign
  //   used with MUX to determine final sign of TC
endmodule

module multiply_by_10 (
  input  [3:0] in_1,
  output [6:0] out_2
);

  Adder #(.width(7)) adder_1 (.a({in_1, 3'b000}), .b({2'b00, in_1, 1'b0}), .out(out_2));  // open: cin, cout
  // Probe on out_2

  // Notes on the sheet:
  //   multiply num by 10: x << 3 + x << 1
endmodule

module conv_digits (
  input  [3:0] in_1,
  input  [3:0] in_2,
  output [6:0] out_3
);

  wire [6:0] multiply_by_10_1_out_2;

  multiply_by_10 multiply_by_10_1 (.in_1(in_1), .out_2(multiply_by_10_1_out_2));
  Adder #(.width(7)) adder_1 (.a(multiply_by_10_1_out_2), .b({3'b000, in_2}), .out(out_3));  // open: cin, cout
  // Probe on out_3
endmodule
