// Logisim project da1_task3.circ as structural Verilog: 7 circuits, main circuit DUT
module DUT (
  input  X,
  input  CLK,
  input  RST,
  output Z
);

  wire next_state_logic_1_t0, next_state_logic_1_t1, next_state_logic_1_t2, Q0, Q1, Q2;

  next_state_logic next_state_logic_1 (
    .x(X), .Q2(Q2), .Q1(Q1), .Q0(Q0), .rst(RST), .z(Z), .T2(next_state_logic_1_t2),
    .T1(next_state_logic_1_t1), .T0(next_state_logic_1_t0));
  T_Flip_Flop T2 (.T(next_state_logic_1_t2), .clk(CLK), .Q(Q2));  // open: Qn, reset, preset
  T_Flip_Flop T1 (.T(next_state_logic_1_t1), .clk(CLK), .Q(Q1));  // open: Qn, reset, preset
  T_Flip_Flop T0 (.T(next_state_logic_1_t0), .clk(CLK), .Q(Q0));  // open: Qn, reset, preset

  // Other names for the same wires on the sheet: z_out = Z

  // Notes on the sheet:
  //   Please put your deisgn below. You may also use subcircuits.
  //   However, do not move, rename, add, or delete any pins.
  //   Put your design below and wire it up to the pins.
  //   Feel free to remove this text.
endmodule

module TB (
);

  wire clk_out, mypor_1_p2, not_1_out, or_1_out, RESET_out, TimeIndex_carry, undriven;
  wire [0:0] dut_1_z;
  wire [4:0] TimeIndex_q;

  Clock #(.highDuration(2), .lowDuration(2)) clk (.out(clk_out));
  Clock sysclk ();  // open: out
  Counter #(.max('h1f), .ongoal("stay"), .width(5)) TimeIndex (
    .load(or_1_out), .clk(clk_out), .D({5{1'b0}}), .carry(TimeIndex_carry), .Q(TimeIndex_q));  // open: clr, up, count
  // MyPOR mypor_1: pin names not known; wires that end beside it: clk_out, mypor_1_p2
  Button RESET (.out(RESET_out));
  ROM #(.addrWidth(5), .dataWidth(1)) TestTraceMemory (.addr(TimeIndex_q));  // open: data
  or or_1 (or_1_out, mypor_1_p2, RESET_out);
  not not_1 (not_1_out, TimeIndex_carry);
  DUT dut_1 (.X(undriven), .CLK(clk_out), .RST(or_1_out), .Z(dut_1_z[0]));
  TTY tty_1 (.data({6'b011000, dut_1_z[0]}), .clk(clk_out), .we(not_1_out), .clr(or_1_out));
  LED DONE (.in(TimeIndex_carry));

  // Notes on the sheet:
  //   DO NOT MODIFY THIS
  //   YOU MAY TEST YOUR CIRCUITS USING THIS TO MAKE SURE YOU HAVE NOT ALTERED PIN OUT
  //   Edit ROM with input trace of 32 bits
  //   contents of TestTraceMemory (hex, n*v repeats v):
  //   1 1 1 0 1 0 0 0 1 1
endmodule

module TBRANDOM (
);

  wire clk_out, mypor_1_p2, not_1_out, or_1_out, random_1_out, RESET_out, TimeIndex_carry;
  wire [0:0] dut_1_z;

  Clock #(.highDuration(2), .lowDuration(2)) clk (.out(clk_out));
  Clock sysclk ();  // open: out
  Counter #(.ongoal("stay")) TimeIndex (
    .load(or_1_out), .clk(clk_out), .D({8{1'b0}}), .carry(TimeIndex_carry));  // open: clr, up, count, Q
  // MyPOR mypor_1: pin names not known; wires that end beside it: clk_out, mypor_1_p2
  Button RESET (.out(RESET_out));
  or or_1 (or_1_out, mypor_1_p2, RESET_out);
  Random #(.width(1)) random_1 (.clr(or_1_out), .clk(clk_out), .out(random_1_out));  // open: next
  not not_1 (not_1_out, TimeIndex_carry);
  DUT dut_1 (.X(random_1_out), .CLK(clk_out), .RST(or_1_out), .Z(dut_1_z[0]));
  TTY tty_1 (.data({6'b011000, dut_1_z[0]}), .clk(clk_out), .we(not_1_out), .clr(or_1_out));
  LED DONE (.in(TimeIndex_carry));

  // Notes on the sheet:
  //   DO NOT MODIFY THIS
  //   YOU MAY TEST YOUR CIRCUITS USING THIS TO MAKE SURE YOU HAVE NOT ALTERED PIN OUT
endmodule

module budgetAND (
  input  in_1,
  input  in_2,
  output out_3
);

  wire nand_1_out;

  nand nand_1 (nand_1_out, in_1, in_2);
  not not_1 (out_3, nand_1_out);
endmodule

module budgetOR (
  input  in_1,
  input  in_2,
  output out_3
);

  wire not_1_out, not_2_out;

  not not_1 (not_1_out, in_1);
  not not_2 (not_2_out, in_2);
  nand nand_1 (out_3, not_1_out, not_2_out);
endmodule

module selector2 (
  input  in_1,
  input  in_2,
  input  in_3,
  output out_4
);

  wire budgetand_1_out_3, budgetand_2_out_3, not_1_out;

  not not_1 (not_1_out, in_3);
  budgetAND budgetand_1 (.in_1(in_1), .in_2(not_1_out), .out_3(budgetand_1_out_3));
  budgetAND budgetand_2 (.in_1(in_2), .in_2(in_3), .out_3(budgetand_2_out_3));
  budgetOR budgetor_1 (.in_1(budgetand_1_out_3), .in_2(budgetand_2_out_3), .out_3(out_4));
endmodule

module next_state_logic (
  input  x,
  input  Q2,
  input  Q1,
  input  Q0,
  input  rst,
  output z,
  output T2,
  output T1,
  output T0
);

  wire nand_1_out, nand_2_out, nand_3_out, nand_4_out, nand_5_out, nand_6_out, nand_7_out, nand_8_out,
       nand_9_out, nand_10_out, nand_11_out, nand_12_out, nand_13_out, nand_14_out, not_1_out, not_2_out,
       not_3_out, not_4_out;

  not not_1 (not_1_out, x);
  not not_2 (not_2_out, Q2);
  not not_3 (not_3_out, Q1);
  not not_4 (not_4_out, Q0);
  nand nand_1 (nand_1_out, not_2_out, not_3_out, Q0);
  nand nand_2 (nand_2_out, Q1, not_4_out);
  nand nand_3 (nand_3_out, x, not_3_out, Q0);
  nand nand_4 (nand_4_out, x, not_2_out, not_3_out);
  nand nand_5 (nand_5_out, Q2, Q0);
  nand nand_6 (nand_6_out, x, Q2);
  nand nand_7 (nand_7_out, not_1_out, not_3_out, not_4_out);
  nand nand_8 (nand_8_out, not_1_out, Q1, Q0);
  nand nand_9 (nand_9_out, x, not_3_out, Q0);
  nand nand_10 (nand_10_out, x, Q1, not_4_out);
  nand nand_11 (nand_11_out, not_1_out, Q2, not_4_out);
  not not_5 (z, nand_1_out);
  nand nand_12 (nand_12_out, nand_2_out, nand_3_out, nand_4_out);
  nand nand_13 (nand_13_out, nand_5_out, nand_6_out);
  nand nand_14 (nand_14_out, nand_7_out, nand_8_out, nand_9_out, nand_10_out, nand_11_out);
  selector2 selector2_1 (.in_1(nand_12_out), .in_2(Q2), .in_3(rst), .out_4(T2));
  selector2 selector2_2 (.in_1(nand_13_out), .in_2(Q1), .in_3(rst), .out_4(T1));
  selector2 selector2_3 (.in_1(nand_14_out), .in_2(Q0), .in_3(rst), .out_4(T0));
endmodule
