// Logisim project da1_task4.circ as structural Verilog: 6 circuits, main circuit DUT
module DUT (
  input  [15:0] DIN1,
  input  [15:0] DIN2,
  input  [15:0] DIN3,
  input  GO1,
  input  GO2,
  input  GO3,
  input  CLK,
  input  RST,
  output [15:0] DOUT,
  output DONE
);

  wire cD3, D0, D1, D2, D3, d_ff_2_q, d_ff_3_q, d_ff_4_q, gt, lt, rdy, sel1, sel2;
  wire [15:0] bit_extender_1_out, med, nand_2_out, nand_3_out, not_1_out, val3;

  assign bit_extender_1_out = {{15{cD3}}, cD3};  // Bit_Extender bit_extender_1
  assign DOUT = ~(nand_2_out & nand_3_out);  // NAND_Gate nand_1, 16 bits wide
  assign nand_2_out = ~(med & not_1_out);  // NAND_Gate nand_2, 16 bits wide
  assign nand_3_out = ~(bit_extender_1_out & val3);  // NAND_Gate nand_3, 16 bits wide
  assign not_1_out = ~bit_extender_1_out;  // NOT_Gate not_1, 16 bits wide
  D_Flip_Flop d_ff_1 (.D(D3), .clk(CLK), .Q(cD3));  // open: Qn, preset, reset
  D_Flip_Flop d_ff_2 (.D(D2), .clk(CLK), .Q(d_ff_2_q));  // open: Qn, preset, reset
  D_Flip_Flop d_ff_3 (.D(D1), .clk(CLK), .Q(d_ff_3_q));  // open: Qn, preset, reset
  D_Flip_Flop d_ff_4 (.D(D0), .clk(CLK), .Q(d_ff_4_q));  // open: Qn, preset, reset
  datapath datapath_1 (
    .CLK(CLK), .RST(RST), .sel1(sel1), .sel2(sel2), .DIN1(DIN1), .GO1(GO1), .DIN2(DIN2), .GO2(GO2),
    .DIN3(DIN3), .GO3(GO3), .done(DONE), .median(med), .gt(gt), .lt(lt), .rdy(rdy), .val3(val3));
  controller controller_1 (
    .D3(cD3), .D2(d_ff_2_q), .D1(d_ff_3_q), .D0(d_ff_4_q), .gt(gt), .lt(lt), .rdy(rdy), .rst(RST),
    .sel1(sel1), .sel2(sel2), .done(DONE), .D3n(D3), .D2n(D2), .D1n(D1), .D0n(D0));

  // Notes on the sheet:
  //   median depends on state, use bit manipulation
  //   Please put your design below. You may also use subcircuits.
  //   However, do not move, rename, add, or delete any pins.
endmodule

module TB (
  input  [15:0] DIN1,
  input  [15:0] DIN2,
  input  [15:0] DIN3,
  input  GO1,
  input  GO2,
  input  GO3,
  input  RST,
  output [15:0] DOUT,
  output DONE
);

  wire clk_out, or_1_out, RESET_out;

  Clock sysclk ();  // open: out
  Button RESET (.out(RESET_out));
  Clock #(.highDuration(2), .lowDuration(2)) clk (.out(clk_out));
  or or_1 (or_1_out, RESET_out, RST);
  DUT dut_1 (
    .DIN1(DIN1), .DIN2(DIN2), .DIN3(DIN3), .GO1(GO1), .GO2(GO2), .GO3(GO3), .CLK(clk_out), .RST(or_1_out),
    .DOUT(DOUT), .DONE(DONE));

  // Notes on the sheet:
  //   DO NOT MODIFY THIS
  //   YOU MAY TEST YOUR CIRCUITS USING THIS TO MAKE SURE YOU HAVE NOT ALTERED PIN OUT
endmodule

module datapath (
  input  CLK,
  input  RST,
  input  sel1,
  input  sel2,
  input  [15:0] DIN1,
  input  GO1,
  input  [15:0] DIN2,
  input  GO2,
  input  [15:0] DIN3,
  input  GO3,
  input  done,
  output [15:0] median,
  output gt,
  output lt,
  output rdy,
  output [15:0] val3
);

  wire budgetand_1_out_3, budgetand_2_out_3, budgetand_3_out_3, budgetor_1_out_3, budgetor_2_out_3,
       budgetor_3_out_3, budgetor_4_out_3, nand_1_out, not_1_out, register_1_q, register_2_q, register_3_q;
  wire [15:0] A_q, B_q, C_q;

  not not_1 (not_1_out, RST);
  budgetAND budgetand_1 (.in_1(GO1), .in_2(not_1_out), .out_3(budgetand_1_out_3));
  budgetOR budgetor_1 (.in_1(RST), .in_2(done), .out_3(budgetor_1_out_3));
  budgetAND budgetand_2 (.in_1(GO2), .in_2(not_1_out), .out_3(budgetand_2_out_3));
  budgetAND budgetand_3 (.in_1(GO3), .in_2(not_1_out), .out_3(budgetand_3_out_3));
  budgetOR budgetor_2 (.in_1(budgetor_1_out_3), .in_2(GO1), .out_3(budgetor_2_out_3));
  budgetOR budgetor_3 (.in_1(budgetor_1_out_3), .in_2(GO2), .out_3(budgetor_3_out_3));
  budgetOR budgetor_4 (.in_1(budgetor_1_out_3), .in_2(GO3), .out_3(budgetor_4_out_3));
  Register #(.width(1)) register_1 (
    .D(budgetand_1_out_3), .en(budgetor_2_out_3), .clk(CLK), .Q(register_1_q));  // open: clr
  Register #(.width(1)) register_2 (
    .D(budgetand_2_out_3), .en(budgetor_3_out_3), .clk(CLK), .Q(register_2_q));  // open: clr
  Register #(.width(1)) register_3 (
    .D(budgetand_3_out_3), .en(budgetor_4_out_3), .clk(CLK), .Q(register_3_q));  // open: clr
  nand nand_1 (nand_1_out, register_1_q, register_2_q, register_3_q);
  not not_2 (rdy, nand_1_out);
  Register #(.width(16)) A (.D(DIN1), .en(rdy), .clk(CLK), .Q(A_q));  // open: clr
  Register #(.width(16)) B (.D(DIN2), .en(rdy), .clk(CLK), .Q(B_q));  // open: clr
  Register #(.width(16)) C (.D(DIN3), .en(rdy), .clk(CLK), .Q(C_q));  // open: clr
  Multiplexer #(.width(16)) multiplexer_1 (.in0(A_q), .in1(B_q), .out(median), .sel(sel1));
  Multiplexer #(.width(16)) multiplexer_2 (.in0(B_q), .in1(C_q), .out(val3), .sel(sel2));
  Comparator #(.width(16)) comparator_1 (.a(median), .b(val3), .gt(gt), .lt(lt));  // open: eq

  // Notes on the sheet:
  //   we need to wait until all 3 DIN's have been loaded, then we tell controller we are ready to ball
  //   comparisons done over multiple clock cycles because of the 3rd variable
endmodule

module budgetAND (
  input  in_1,
  input  in_2,
  output out_3
);

  wire nand_1_out;

  nand nand_1 (nand_1_out, in_1, in_2);
  not not_1 (out_3, nand_1_out);
endmodule

module budgetOR (
  input  in_1,
  input  in_2,
  output out_3
);

  wire not_1_out, not_2_out;

  not not_1 (not_1_out, in_1);
  not not_2 (not_2_out, in_2);
  nand nand_1 (out_3, not_1_out, not_2_out);
endmodule

module controller (
  input  D3,
  input  D2,
  input  D1,
  input  D0,
  input  gt,
  input  lt,
  input  rdy,
  input  rst,
  output sel1,
  output sel2,
  output done,
  output D3n,
  output D2n,
  output D1n,
  output D0n
);

  wire nand_1_out, nand_2_out, nand_3_out, nand_5_out, nand_6_out, nand_7_out, nand_8_out, nand_9_out,
       nand_10_out, nand_11_out, nand_12_out, nand_13_out, nand_14_out, nand_15_out, nand_16_out,
       nand_17_out, nand_18_out, nand_21_out, nand_22_out, nand_23_out, nand_24_out, not_1_out, not_2_out,
       not_3_out, not_4_out, not_5_out, not_6_out, not_7_out;

  not not_1 (not_1_out, gt);
  not not_2 (not_2_out, lt);
  not not_3 (not_3_out, D3);
  not not_4 (not_4_out, D2);
  not not_5 (not_5_out, D1);
  not not_6 (not_6_out, D0);
  nand nand_1 (nand_1_out, D1, D0);
  nand nand_2 (nand_2_out, D2, D1);
  nand nand_3 (nand_3_out, D3, not_5_out);
  nand nand_4 (sel2, not_5_out, not_3_out);
  nand nand_5 (nand_5_out, D3, not_5_out, not_6_out);
  nand nand_6 (nand_6_out, not_2_out, not_3_out, not_4_out, D1);
  nand nand_7 (nand_7_out, not_1_out, D3, D0);
  nand nand_8 (nand_8_out, not_1_out, D3, D1);
  nand nand_9 (nand_9_out, lt, not_3_out, not_4_out, D1);
  nand nand_10 (nand_10_out, gt, D3, D0);
  nand nand_11 (nand_11_out, gt, D3, D1);
  nand nand_12 (nand_12_out, not_3_out, not_4_out, D0);
  nand nand_13 (nand_13_out, gt, not_4_out, D0);
  nand nand_14 (nand_14_out, not_1_out, not_3_out, not_4_out, not_5_out, D0);
  nand nand_15 (nand_15_out, not_2_out, not_3_out, not_4_out, D1, not_6_out);
  nand nand_16 (nand_16_out, gt, D3, D0);
  nand nand_17 (nand_17_out, gt, D3, D1);
  nand nand_18 (nand_18_out, rdy, not_3_out, not_4_out, not_5_out, not_6_out);
  nand nand_19 (sel1, nand_1_out, nand_2_out, nand_3_out);
  nand nand_20 (done, not_4_out, nand_5_out);
  nand nand_21 (nand_21_out, nand_6_out, nand_7_out, nand_8_out);
  nand nand_22 (nand_22_out, nand_9_out, nand_10_out, nand_11_out);
  nand nand_23 (nand_23_out, nand_12_out, nand_13_out);
  nand nand_24 (nand_24_out, nand_14_out, nand_15_out, nand_16_out, nand_17_out, nand_18_out);
  not not_7 (not_7_out, rst);
  budgetAND budgetand_1 (.in_1(nand_21_out), .in_2(not_7_out), .out_3(D3n));
  budgetAND budgetand_2 (.in_1(nand_22_out), .in_2(not_7_out), .out_3(D2n));
  budgetAND budgetand_3 (.in_1(nand_23_out), .in_2(not_7_out), .out_3(D1n));
  budgetAND budgetand_4 (.in_1(nand_24_out), .in_2(not_7_out), .out_3(D0n));

  // Notes on the sheet:
  //   basic fsm type stuff
endmodule
