// Logisim project other.circ as structural Verilog: 2 circuits, main circuit DUT
// FINISHED
module DUT (
  input  [15:0] DIN1,
  input  [15:0] DIN2,
  input  [15:0] DIN3,
  input  GO1,
  input  GO2,
  input  GO3,
  input  CLK,
  input  RST,
  output [15:0] DOUT,
  output DONE
);

  wire CONDITION_2, CONDITION_3, CONDITION_4_1, CONDITION_4_2, d_ff_1_qn, d_ff_2_qn, d_ff_3_qn, LT,
       nand_1_out, nand_2_out, nand_3_out, nand_4_out, nand_6_out, nand_10_out, nand_11_out, nand_12_out,
       nand_14_out, nand_15_out, nand_18_out, nand_20_out, nand_23_out, nand_24_out, nand_25_out,
       nand_26_out, nand_27_out, nand_28_out, not_1_out, not_2_out, not_3_out, not_4_out, not_5_out,
       not_6_out, not_7_out, not_8_out, not_9_out, not_10_out, not_11_out, not_12_out, not_13_out,
       not_14_out, not_18_out, not_19_out, not_20_out, not_21_out, not_22_out, not_24_out, not_26_out,
       not_27_out, not_28_out, not_29_out, not_49_out, PREV_SUM_LT_ONE_NOT_3, PREV_SUM_LT_ZERO_NOT_3, REDO,
       SUM_LT_0, SUM_LT_1;
  wire [1:0] C1, C2, nand_16_out, nand_31_out, nand_32_out, nand_37_out, nand_38_out, nand_39_out,
       nand_40_out, not_33_out, not_34_out, not_35_out, not_36_out, not_44_out, not_45_out, PREV_SUM_LT_ONE,
       PREV_SUM_LT_ONE_n, PREV_SUM_LT_ONE_n0, PREV_SUM_LT_ZERO, PREV_SUM_LT_ZERO_n, PREV_SUM_LT_ZERO_n0,
       PSLTON, PSLTZN, SLTN, SUM_LT;
  wire [1:1] not_23_out, SUM_LT_n, UPDATE_MASK, UPDATE_SUM_LT_ZERO_MASK;
  wire [2:0] P;
  wire [15:0] A, B, bit_extender_1_out, bit_extender_2_out, C, multiplexer_1_out, multiplexer_2_out,
       nand_7_out, nand_8_out, nand_29_out, nand_30_out, nand_35_out, nand_36_out, nand_41_out, nand_42_out,
       nand_46_out, nand_47_out, not_15_out, not_30_out, not_43_out, not_50_out, NUM1, NUM2,
       NUM_PREV_SUM_LT_ONE;

  Register #(.width(2)) u_SUM_LT (.D(SLTN), .en(1'b1), .clk(CLK), .Q(SUM_LT));  // open: clr
  Multiplexer #(.width(16)) multiplexer_1 (.in0(C), .in1(B), .out(multiplexer_1_out), .sel(C1[0]));
  not not_1 (not_1_out, C1[1]);
  not not_2 (not_2_out, P[2]);
  not not_3 (not_3_out, C1[0]);
  not not_4 (not_4_out, C1[0]);
  not not_5 (not_5_out, P[0]);
  not not_6 (not_6_out, P[2]);
  not not_7 (not_7_out, C1[0]);
  not not_8 (not_8_out, P[0]);
  not not_9 (not_9_out, GO1);
  not not_10 (not_10_out, GO2);
  not not_11 (not_11_out, GO2);
  not not_12 (not_12_out, RST);
  not not_13 (not_13_out, P[0]);
  not not_14 (not_14_out, REDO);
  Register #(.width(16)) u_A (.D(DIN1), .en(GO1), .clk(CLK), .Q(A));  // open: clr
  assign not_15_out = ~bit_extender_1_out;  // NOT_Gate not_15, 16 bits wide
  assign bit_extender_1_out = {{15{not_1_out}}, not_1_out};  // Bit_Extender bit_extender_1
  nand nand_1 (nand_1_out, not_2_out, not_3_out);
  not not_16 (C1[1], nand_1_out);
  nand nand_2 (nand_2_out, P[0], not_4_out, P[2]);
  nand nand_3 (nand_3_out, not_5_out, C1[0], not_6_out);
  nand nand_4 (nand_4_out, not_7_out, not_8_out);
  not not_17 (C2[0], nand_4_out);
  not not_18 (not_18_out, SUM_LT_1);
  not not_19 (not_19_out, SUM_LT_n[1]);
  not not_20 (not_20_out, DONE);
  not not_21 (not_21_out, SUM_LT_1);
  not not_22 (not_22_out, SUM_LT_n[1]);
  nand nand_5 (REDO, not_9_out, not_10_out, not_11_out, not_12_out);
  nand nand_6 (nand_6_out, not_13_out, not_14_out);
  not not_23 (not_23_out[1], nand_6_out);
  assign nand_7_out = ~(A & not_15_out);  // NAND_Gate nand_7, 16 bits wide
  assign nand_8_out = ~(multiplexer_1_out & bit_extender_1_out);  // NAND_Gate nand_8, 16 bits wide
  nand nand_9 (C2[1], nand_2_out, nand_3_out);
  Comparator #(.width(16)) comparator_1 (.a(NUM2), .b(NUM1), .gt(LT));  // open: eq, lt
  nand nand_10 (nand_10_out, SUM_LT[0], LT);
  nand nand_11 (nand_11_out, LT, SUM_LT[0]);
  not not_24 (not_24_out, SUM_LT[1]);
  nand nand_12 (nand_12_out, not_18_out, not_19_out);
  not not_25 (SUM_LT_0, nand_12_out);
  nand nand_13 (PREV_SUM_LT_ONE_NOT_3, PREV_SUM_LT_ONE[0], PREV_SUM_LT_ONE[1]);
  not not_26 (not_26_out, CONDITION_2);
  not not_27 (not_27_out, CONDITION_3);
  not not_28 (not_28_out, CONDITION_4_1);
  not not_29 (not_29_out, CONDITION_4_2);
  assign not_30_out = ~{16{CONDITION_4_2}};  // NOT_Gate not_30, 16 bits wide
  nand nand_14 (nand_14_out, P[0], not_20_out);
  not not_31 (UPDATE_MASK[1], nand_14_out);
  nand nand_15 (nand_15_out, not_21_out, not_22_out);
  not not_32 (UPDATE_SUM_LT_ZERO_MASK[1], nand_15_out);
  assign nand_16_out = ~({SUM_LT_n[1], SUM_LT_1} & {2{not_23_out[1]}});  // NAND_Gate nand_16, 2 bits wide
  assign not_33_out = ~{2{REDO}};  // NOT_Gate not_33, 2 bits wide
  assign not_34_out = ~PREV_SUM_LT_ZERO_n;  // NOT_Gate not_34, 2 bits wide
  assign not_35_out = ~{2{REDO}};  // NOT_Gate not_35, 2 bits wide
  assign not_36_out = ~PREV_SUM_LT_ONE_n;  // NOT_Gate not_36, 2 bits wide
  Register #(.width(16)) u_B (.D(DIN2), .en(GO2), .clk(CLK), .Q(B));  // open: clr
  Register #(.width(2)) u_PREV_SUM_LT_ZERO (.D(PSLTZN), .en(1'b1), .clk(CLK), .Q(PREV_SUM_LT_ZERO));  // open: clr
  assign NUM1 = ~(nand_7_out & nand_8_out);  // NAND_Gate nand_17, 16 bits wide
  nand nand_18 (nand_18_out, SUM_LT[0], nand_10_out);
  nand nand_19 (SUM_LT_1, nand_18_out, nand_20_out);
  nand nand_20 (nand_20_out, nand_10_out, LT);
  nand nand_21 (SUM_LT_n[1], nand_11_out, not_24_out);
  nand nand_22 (PREV_SUM_LT_ZERO_NOT_3, PREV_SUM_LT_ZERO[0], PREV_SUM_LT_ZERO[1]);
  nand nand_23 (nand_23_out, SUM_LT_1, PREV_SUM_LT_ONE_NOT_3);
  not not_37 (CONDITION_2, nand_23_out);
  nand nand_24 (nand_24_out, SUM_LT_0, PREV_SUM_LT_ZERO_NOT_3);
  nand nand_25 (nand_25_out, SUM_LT_1, PREV_SUM_LT_ZERO_NOT_3);
  nand nand_26 (nand_26_out, SUM_LT_0, PREV_SUM_LT_ONE_NOT_3);
  nand nand_27 (nand_27_out, P[0], nand_28_out);
  nand nand_28 (nand_28_out, not_26_out, not_27_out, not_28_out, not_29_out);
  assign nand_29_out = ~(NUM_PREV_SUM_LT_ONE & {16{CONDITION_4_2}});  // NAND_Gate nand_29, 16 bits wide
  assign nand_30_out = ~(not_30_out & NUM1);  // NAND_Gate nand_30, 16 bits wide
  assign nand_31_out = ~({2{UPDATE_MASK[1]}} & {2{SUM_LT_1}});  // NAND_Gate nand_31, 2 bits wide
  assign nand_32_out = ~({2{UPDATE_MASK[1]}} & {2{UPDATE_SUM_LT_ZERO_MASK[1]}});  // NAND_Gate nand_32, 2 bits wide
  assign SLTN = ~nand_16_out;  // NOT_Gate not_38, 2 bits wide
  assign PSLTZN = ~(not_33_out & not_34_out);  // NAND_Gate nand_33, 2 bits wide
  assign PSLTON = ~(not_35_out & not_36_out);  // NAND_Gate nand_34, 2 bits wide
  not not_39 (CONDITION_3, nand_24_out);
  not not_40 (CONDITION_4_1, nand_25_out);
  not not_41 (CONDITION_4_2, nand_26_out);
  not not_42 (DONE, nand_27_out);
  assign not_43_out = ~{16{PREV_SUM_LT_ONE[0]}};  // NOT_Gate not_43, 16 bits wide
  assign nand_35_out = ~({16{DONE}} & nand_36_out);  // NAND_Gate nand_35, 16 bits wide
  assign nand_36_out = ~(nand_29_out & nand_30_out);  // NAND_Gate nand_36, 16 bits wide
  assign nand_37_out = ~(PREV_SUM_LT_ONE & nand_31_out);  // NAND_Gate nand_37, 2 bits wide
  assign nand_38_out = ~(PREV_SUM_LT_ZERO & nand_32_out);  // NAND_Gate nand_38, 2 bits wide
  assign not_44_out = ~PREV_SUM_LT_ONE_n0;  // NOT_Gate not_44, 2 bits wide
  assign nand_39_out = ~({2{UPDATE_MASK[1]}} & {2{SUM_LT_1}} & C1);  // NAND_Gate nand_39, 2 bits wide
  assign not_45_out = ~PREV_SUM_LT_ZERO_n0;  // NOT_Gate not_45, 2 bits wide
  assign nand_40_out = ~({2{UPDATE_MASK[1]}} & {2{UPDATE_SUM_LT_ZERO_MASK[1]}} & C1);  // NAND_Gate nand_40, 2 bits wide
  assign nand_41_out = ~(A & not_43_out);  // NAND_Gate nand_41, 16 bits wide
  assign nand_42_out = ~(B & {16{PREV_SUM_LT_ONE[0]}});  // NAND_Gate nand_42, 16 bits wide
  assign DOUT = ~nand_35_out;  // NOT_Gate not_46, 16 bits wide
  assign PREV_SUM_LT_ONE_n0 = ~nand_37_out;  // NOT_Gate not_47, 2 bits wide
  assign PREV_SUM_LT_ZERO_n0 = ~nand_38_out;  // NOT_Gate not_48, 2 bits wide
  assign PREV_SUM_LT_ONE_n = ~(not_44_out & nand_39_out);  // NAND_Gate nand_43, 2 bits wide
  assign PREV_SUM_LT_ZERO_n = ~(not_45_out & nand_40_out);  // NAND_Gate nand_44, 2 bits wide
  Register #(.width(16)) u_C (.D(DIN3), .en(GO3), .clk(CLK), .Q(C));  // open: clr
  Multiplexer #(.width(16)) multiplexer_2 (.in0(C), .in1(B), .out(multiplexer_2_out), .sel(C2[0]));
  assign bit_extender_2_out = {{15{not_49_out}}, not_49_out};  // Bit_Extender bit_extender_2
  not not_49 (not_49_out, C2[1]);
  assign NUM_PREV_SUM_LT_ONE = ~(nand_41_out & nand_42_out);  // NAND_Gate nand_45, 16 bits wide
  assign not_50_out = ~bit_extender_2_out;  // NOT_Gate not_50, 16 bits wide
  Register #(.width(2)) u_PREV_SUM_LT_ONE (.D(PSLTON), .en(1'b1), .clk(CLK), .Q(PREV_SUM_LT_ONE));  // open: clr
  assign nand_46_out = ~(A & not_50_out);  // NAND_Gate nand_46, 16 bits wide
  assign nand_47_out = ~(multiplexer_2_out & bit_extender_2_out);  // NAND_Gate nand_47, 16 bits wide
  assign NUM2 = ~(nand_46_out & nand_47_out);  // NAND_Gate nand_48, 16 bits wide
  D_Flip_Flop d_ff_1 (.D(d_ff_1_qn), .clk(CLK), .Q(P[0]), .Qn(d_ff_1_qn), .reset(REDO));  // open: preset
  D_Flip_Flop d_ff_2 (.D(d_ff_2_qn), .clk(d_ff_1_qn), .Q(C1[0]), .Qn(d_ff_2_qn), .reset(REDO));  // open: preset
  D_Flip_Flop d_ff_3 (.D(d_ff_3_qn), .clk(d_ff_2_qn), .Q(P[2]), .Qn(d_ff_3_qn), .reset(REDO));  // open: preset

  // Other names for the same wires on the sheet: CONDITION_4_2_MASK[15:0] = {16{CONDITION_4_2}};
  //   MEDIAN_n[15:0] = DOUT; TIME_TO_CHECK = P[0]; P[1] = C1[0]; P1 = C1[0]; SEL_NUM1[1:0] = C1; SEL_NUM2[1:0] = C2;
  //   UPDATE_MASK[0] = UPDATE_MASK[1]; FINISHED = DONE; UPDATE_MEDIAN_MASK[15:0] = {16{DONE}}; SUM_LT_n[0] = SUM_LT_1;
  //   UPDATE_SUM_LT_ONE_MASK[1:0] = {2{SUM_LT_1}}; UPDATE_SUM_LT_ZERO_MASK[0] = UPDATE_SUM_LT_ZERO_MASK[1]

  // Notes on the sheet:
  //   MEMORY
  //   CALCULATING ADDRESSES
  //   EXECUTING THE COMPARISON
  //   STOPPING CONDITIONS
  //   UPDATE THE LT FLAGS
  //   RESET BEHAVIOR
  //   3 to 1 MUX to select the number to operate on
  //   Increment the sum by the result of the comparison C1 < C2
  //   Reset the LT flags if they need to be updated
  //   Update the LT flags if they need to be updated
  //   Derive the address of the number to compare from phase number
  //   Derive the address of the second number to compare from phase number
  //   Select the right numbers to compare and compare them C1 < C2
  //   Please put your design below. You may also use subcircuits.
  //   However, do not move, rename, add, or delete any pins.
  //   3 to 1 MUX to select the number to operate on
endmodule

module TB (
  input  [15:0] DIN1,
  input  [15:0] DIN2,
  input  [15:0] DIN3,
  input  GO1,
  input  GO2,
  input  GO3,
  input  RST,
  output [15:0] DOUT,
  output DONE
);

  wire clk_out, or_1_out, RESET_out;

  Clock sysclk ();  // open: out
  Button RESET (.out(RESET_out));
  Clock #(.highDuration(2), .lowDuration(2)) clk (.out(clk_out));
  or or_1 (or_1_out, RESET_out, RST);
  DUT dut_1 (
    .DIN1(DIN1), .DIN2(DIN2), .DIN3(DIN3), .GO1(GO1), .GO2(GO2), .GO3(GO3), .CLK(clk_out), .RST(or_1_out),
    .DOUT(DOUT), .DONE(DONE));

  // Notes on the sheet:
  //   DO NOT MODIFY THIS
  //   YOU MAY TEST YOUR CIRCUITS USING THIS TO MAKE SURE YOU HAVE NOT ALTERED PIN OUT
endmodule
